// Logisim project yatzy.circ as structural Verilog
module main (
  input  in_1,
  input  in_2,
  input  in_3,
  input  in_4,
  output out_5,
  output out_6,
  output out_7,
  output out_8,
  output out_9,
  output out_10,
  output out_11,
  output out_12,
  output out_13,
  output out_14,
  output out_15,
  output out_16,
  output out_17,
  output out_18,
  output out_19,
  output out_20,
  output out_21,
  output out_22,
  output out_23,
  output out_24,
  output out_25,
  output out_26,
  output out_27,
  output out_28,
  output out_29,
  output out_30,
  output out_31,
  output out_32,
  output out_33,
  output out_34,
  output out_35,
  output out_36
);

  wire _11, _12, _13, _14, _15, _21, _22, _23, _24, _25, and_1_out, and_2_out, and_3_out, and_6_out,
       and_7_out, and_8_out, and_9_out, and_10_out, and_12_out, and_13_out, await_sol, buffer_1_out,
       button_6_out, button_7_out, button_8_out, button_9_out, button_10_out, button_11_out, button_12_out,
       button_13_out, button_14_out, button_15_out, button_16_out, button_17_out, cdm_16_1_p4, cdm_16_1_p5,
       cdm_16_1_p6, cdm_16_1_p7, cdm_16_1_p8, cdm_16_1_p10, cdm_16_1_p15, cIk, clk, clock_1_out, clock_2_out,
       counter_1_carry, counter_2_carry, counter_3_carry, counter_4_carry, counter_6_carry, counter_7_carry,
       counter_10_carry, counter_11_carry, demultiplexer_1_out0, demultiplexer_1_out1, demultiplexer_1_out2,
       demultiplexer_1_out3, demultiplexer_1_out4, demultiplexer_1_out5, demultiplexer_1_out6,
       demultiplexer_1_out7, demultiplexer_1_out8, demultiplexer_1_out9, demultiplexer_1_out10, done1, done2,
       e, hoId, in1, in2, in3, kok_1_roll_enabled, kok_1_swap, kok_2_roll_enabled, kok_2_swap, m,
       nicesr_1_out_3, not_1_out, not_13_out, not_14_out, not_15_out, not_16_out, not_17_out, not_18_out,
       not_19_out, not_20_out, not_21_out, not_22_out, not_23_out, not_24_out, not_25_out, not_26_out,
       or_1_out, or_2_out, or_4_out, p00o, p01o, p02o, p03o, p04o, p05o, p06o, p07o, p08o, p09o, p10o,
       random_1_out, reroll_bot, start1, start2, start_bot, start_out, t_ff_1_q, tand_4_out_3, tand_5_out_3,
       tand_6_out_3, tand_7_out_3, tand_8_out_3, tand_9_out_3, tand_10_out_3, tand_14_out_3, tand_15_out_3,
       tand_16_out_3, tick_1_out_2, tick_2_out_2, tick_4_out_2, tick_5_out_2, tick_6_out_2, tick_7_out_2,
       tick_8_out_2, tick_9_out_2, tick_10_out_2, tick_11_out_2, tick_12_out_2, tick_13_out_2, tick_14_out_2,
       tick_15_out_2, tick_16_out_2, tick_17_out_2, tick_18_out_2, tor_1_out_3, tor_2_out_3, tor_3_out_3,
       tor_4_out_3, tor_5_out_3, tor_6_out_3, tor_7_out_3, tor_8_out_3, tor_9_out_3, tor_10_out_3,
       tor_11_out_3, tor_12_out_3, tor_13_out_3, tor_14_out_3, tor_15_out_3, tor_16_out_3, tor_17_out_3,
       tor_18_out_3, tor_19_out_3, tor_20_out_3, tor_21_out_3, tt_1_out_2, tt_2_out_2, tt_3_out_2,
       tt_4_out_2, tt_5_out_2, tt_6_out_2, tt_8_out_2, tt_9_out_2, tt_10_out_2, tt_11_out_2, tt_12_out_2,
       tt_13_out_2, tt_14_out_2, tt_15_out_2, tt_fancy_1_out_3, w;
  wire [2:0] kok_1_out_46, kok_1_out_48, kok_1_out_50, kok_1_out_52, kok_1_out_54, \с0 , \с1 , \с2 , \с3 ,
       \с4 ;
  wire [3:0] bit_extender_2_out;
  wire [7:0] controlled_buffer_1_out, kok_1_out_23, kok_1_out_25, kok_1_out_27, kok_1_out_29, kok_1_out_31,
       kok_1_out_33, kok_1_out_35, kok_1_out_37, kok_1_out_39, kok_1_out_41, kok_1_out_43, kok_2_out_23,
       kok_2_out_25, kok_2_out_27, kok_2_out_29, kok_2_out_31, kok_2_out_33, kok_2_out_35, kok_2_out_37,
       kok_2_out_39, kok_2_out_41, kok_2_out_43, ram_1_data;
  wire [10:0] not_2_out;
  wire [15:0] bit_extender_1_out, cdm_16_1_p2, cdm_16_1_p12, cdm_16_1_p13, cdm_16_1_p14,
       controlled_buffer_5_out, controlled_buffer_6_out, controlled_buffer_7_out, pull_resistor_1_node,
       sum_points_1_out_23, sum_points_2_out_23;

  Button start (.out(start_out));
  Counter #(.width(1), .max('h1)) counter_1 (
    .carry(counter_1_carry), .clk(start_out), .clr(counter_1_carry));  // open: load, D, count, Q
  Random #(.width(1)) random_1 (.clk(start_out), .next(start_out), .out(random_1_out));  // open: clr
  Button button_1 (.out(_11));
  Button button_2 (.out(_12));
  Button button_3 (.out(_13));
  Button button_4 (.out(_14));
  Button button_5 (.out(_15));
  tand tand_1 (.in_1(counter_1_carry), .in_2(random_1_out), .out_3(start1));
  tand tand_2 (.in_1(counter_1_carry), .in_2(not_1_out), .out_3(start2));
  not not_1 (not_1_out, random_1_out);
  Button button_6 (.out(button_6_out));
  Button button_7 (.out(button_7_out));
  Button button_8 (.out(button_8_out));
  Button button_9 (.out(button_9_out));
  Button button_10 (.out(button_10_out));
  Button button_11 (.out(button_11_out));
  Button button_12 (.out(button_12_out));
  Button button_13 (.out(button_13_out));
  Button button_14 (.out(button_14_out));
  Button button_15 (.out(button_15_out));
  Button button_16 (.out(button_16_out));
  Button button_17 (.out(button_17_out));
  or or_1 (or_1_out, start1, or_2_out);
  kok kok_1 (
    .in_1(button_6_out), .in_2(button_7_out), .in_3(button_8_out), .in_4(button_9_out), .in_5(button_10_out),
    .in_6(button_11_out), .in_7(button_12_out), .in_8(button_13_out), .in_9(button_14_out),
    .in_10(button_15_out), .in_11(button_16_out), .reset(in_1), .done(done1), .roll(button_17_out),
    .enable(t_ff_1_q), .out_22(out_5), .out_23(kok_1_out_23), .out_24(out_7), .out_25(kok_1_out_25),
    .out_26(out_9), .out_27(kok_1_out_27), .out_28(out_11), .out_29(kok_1_out_29), .out_30(out_13),
    .out_31(kok_1_out_31), .out_32(out_15), .out_33(kok_1_out_33), .out_34(out_17), .out_35(kok_1_out_35),
    .out_36(out_19), .out_37(kok_1_out_37), .out_38(out_21), .out_39(kok_1_out_39), .out_40(out_23),
    .out_41(kok_1_out_41), .out_42(out_25), .out_43(kok_1_out_43), .start(start1), .other_done(done2),
    .out_46(kok_1_out_46), .out_48(kok_1_out_48), .out_50(kok_1_out_50), .out_52(kok_1_out_52),
    .out_54(kok_1_out_54), .swap(kok_1_swap), .in_16(_11), .in_17(_12), .in_18(_13), .in_19(_14),
    .in_20(_15), .out_47(out_27), .out_49(out_29), .out_51(out_31), .out_53(out_33), .out_55(out_35),
    .roll_enabled(kok_1_roll_enabled));
  T_Flip_Flop t_ff_1 (.clk(or_1_out), .T(or_1_out), .Q(t_ff_1_q));  // open: Qn, preset, reset, en
  LED led_1 (.in(t_ff_1_q));
  Counter #(.width(2), .max('h3)) counter_2 (.carry(counter_2_carry), .clk(and_1_out));  // open: load, D, count, Q, clr
  tor tor_1 (.in_1(counter_2_carry), .in_2(tick_1_out_2), .out_3(tor_1_out_3));
  and and_1 (and_1_out, clock_2_out, tor_2_out_3);
  tor tor_2 (.in_1(tt_2_out_2), .in_2(counter_2_carry), .out_3(tor_2_out_3));
  tt tt_1 (.in_1(done1), .out_2(tt_1_out_2));
  or or_2 (or_2_out, kok_1_swap, kok_2_swap);
  not not_2 (not_2_out[0], out_6);
  not not_3 (not_2_out[1], out_8);
  not not_4 (not_2_out[2], out_10);
  not not_5 (not_2_out[3], out_12);
  not not_6 (not_2_out[4], out_14);
  not not_7 (not_2_out[5], out_16);
  not not_8 (not_2_out[6], out_18);
  not not_9 (not_2_out[7], out_20);
  not not_10 (not_2_out[8], out_22);
  not not_11 (not_2_out[9], out_24);
  not not_12 (not_2_out[10], out_26);
  tt tt_2 (.in_1(tor_1_out_3), .out_2(tt_2_out_2));
  and and_2 (and_2_out, clock_2_out, tor_4_out_3);
  // Probe on sum_points_1_out_23
  sum_points sum_points_1 (
    .in_1(out_5), .in_2(out_7), .in_3(out_9), .in_4(out_11), .in_5(out_13), .in_6(out_15), .in_7(out_17),
    .in_8(out_19), .in_9(out_21), .in_10(out_23), .in_11(out_25), .in_12(kok_1_out_23), .in_13(kok_1_out_25),
    .in_14(kok_1_out_27), .in_15(kok_1_out_29), .in_16(kok_1_out_31), .in_17(kok_1_out_33),
    .in_18(kok_1_out_35), .in_19(kok_1_out_37), .in_20(kok_1_out_39), .in_21(kok_1_out_41),
    .in_22(kok_1_out_43), .out_23(sum_points_1_out_23));
  // Probe on kok_1_out_23
  // Probe on kok_1_out_25
  // Probe on kok_1_out_27
  // Probe on kok_1_out_29
  // Probe on kok_1_out_31
  // Probe on kok_1_out_33
  // Probe on kok_1_out_35
  // Probe on kok_1_out_37
  // Probe on kok_1_out_39
  // Probe on kok_1_out_41
  // Probe on kok_1_out_43
  // Probe on kok_1_out_46
  // Probe on kok_1_out_48
  // Probe on kok_1_out_50
  // Probe on kok_1_out_52
  // Probe on kok_1_out_54
  tt tt_3 (.in_1(kok_1_swap), .out_2(tt_3_out_2));
  Counter #(.width(3), .max('h7)) counter_3 (.carry(counter_3_carry), .clk(and_2_out));  // open: load, D, count, Q, clr
  tt tt_4 (.in_1(tor_3_out_3), .out_2(tt_4_out_2));
  tor tor_3 (.in_1(counter_3_carry), .in_2(tick_1_out_2), .out_3(tor_3_out_3));
  tor tor_4 (.in_1(tt_4_out_2), .in_2(counter_3_carry), .out_3(tor_4_out_3));
  Counter #(.width(4), .max('hf)) counter_4 (.carry(counter_4_carry), .clk(and_3_out));  // open: load, D, count, Q, clr
  and and_3 (and_3_out, clock_2_out, tor_5_out_3);
  tor tor_5 (.in_1(tt_5_out_2), .in_2(counter_4_carry), .out_3(tor_5_out_3));
  buf buffer_1 (buffer_1_out, clock_1_out);
  Clock clock_1 (.out(clock_1_out));
  buf buffer_2 (clk, buffer_1_out);
  assign controlled_buffer_1_out = counter_2_carry ? {8{1'b0}} : 8'bz;  // Controlled_Buffer controlled_buffer_1
  assign controlled_buffer_1_out = counter_3_carry ? 8'h5 : 8'bz;  // Controlled_Buffer controlled_buffer_2
  assign controlled_buffer_1_out = counter_4_carry ? 8'hf : 8'bz;  // Controlled_Buffer controlled_buffer_3
  tor tor_6 (.in_1(counter_4_carry), .in_2(tick_1_out_2), .out_3(tor_6_out_3));
  tt tt_5 (.in_1(tor_6_out_3), .out_2(tt_5_out_2));
  tick tick_1 (.in_1(in_4), .out_2(tick_1_out_2));
  kok kok_2 (
    .in_1(p00o), .in_2(p01o), .in_3(p02o), .in_4(p03o), .in_5(p04o), .in_6(p05o), .in_7(p06o), .in_8(p07o),
    .in_9(p08o), .in_10(p09o), .in_11(p10o), .reset(in_2), .done(done2), .roll(start_bot),
    .enable(not_14_out), .out_22(out_6), .out_23(kok_2_out_23), .out_24(out_8), .out_25(kok_2_out_25),
    .out_26(out_10), .out_27(kok_2_out_27), .out_28(out_12), .out_29(kok_2_out_29), .out_30(out_14),
    .out_31(kok_2_out_31), .out_32(out_16), .out_33(kok_2_out_33), .out_34(out_18), .out_35(kok_2_out_35),
    .out_36(out_20), .out_37(kok_2_out_37), .out_38(out_22), .out_39(kok_2_out_39), .out_40(out_24),
    .out_41(kok_2_out_41), .out_42(out_26), .out_43(kok_2_out_43), .start(start2), .other_done(done1),
    .out_46(\с0 ), .out_48(\с1 ), .out_50(\с2 ), .out_52(\с3 ), .out_54(\с4 ), .swap(kok_2_swap),
    .in_16(_21), .in_17(_22), .in_18(_23), .in_19(_24), .in_20(_25), .out_47(out_28), .out_49(out_30),
    .out_51(out_32), .out_53(out_34), .out_55(out_36), .roll_enabled(kok_2_roll_enabled));
  or or_3 (start_bot, reroll_bot, tick_2_out_2);
  tick tick_2 (.in_1(kok_2_roll_enabled), .out_2(tick_2_out_2));
  not not_13 (not_13_out, kok_2_roll_enabled);
  not not_14 (not_14_out, t_ff_1_q);
  and and_4 (e, not_14_out, not_13_out);
  LED led_2 (.in(not_14_out));
  // Probe on cdm_16_1_p2
  // Probe on cdm_16_1_p4
  // CdM_16 cdm_16_1: pin names not known; wires that end beside it: 1'b0, cdm_16_1_p2, cIk, cdm_16_1_p4, cdm_16_1_p5, cdm_16_1_p6, cdm_16_1_p7, cdm_16_1_p8, m, cdm_16_1_p10, w, cdm_16_1_p12, cdm_16_1_p13, cdm_16_1_p14, cdm_16_1_p15
  // Probe on cdm_16_1_p5
  and and_5 (hoId, w, tt_fancy_1_out_3);
  tt_fancy tt_fancy_1 (.in_1(start_bot), .in_2(await_sol), .out_3(tt_fancy_1_out_3));
  tick tick_3 (.in_1(not_15_out), .out_2(await_sol));
  not not_15 (not_15_out, tor_15_out_3);
  tt tt_6 (.in_1(done2), .out_2(tt_6_out_2));
  tt tt_7 (.in_1(kok_2_swap), .out_2(cdm_16_1_p15));
  // Probe on cdm_16_1_p6
  // Probe on cdm_16_1_p7
  // Probe on cdm_16_1_p8
  // Probe on nothing
  assign cdm_16_1_p14 = tand_4_out_3 ? controlled_buffer_7_out : 16'bz;  // Controlled_Buffer controlled_buffer_4
  Counter #(.width(2), .max('h3)) counter_5 (.carry(in1), .clk(and_6_out));  // open: load, D, count, Q, clr
  and and_6 (and_6_out, clk, tor_7_out_3);
  not not_16 (not_16_out, tt_9_out_2);
  tor tor_7 (.in_1(tt_9_out_2), .in_2(in1), .out_3(tor_7_out_3));
  RAM ram_1 (.addr(controlled_buffer_1_out), .data(ram_1_data), .clk(clock_2_out), .ld(1'b0), .clr(in_3));  // open: sel
  Clock clock_2 (.out(clock_2_out));
  // Probe on sum_points_2_out_23
  sum_points sum_points_2 (
    .in_1(out_6), .in_2(out_8), .in_3(out_10), .in_4(out_12), .in_5(out_14), .in_6(out_16), .in_7(out_18),
    .in_8(out_20), .in_9(out_22), .in_10(out_24), .in_11(out_26), .in_12(kok_2_out_23), .in_13(kok_2_out_25),
    .in_14(kok_2_out_27), .in_15(kok_2_out_29), .in_16(kok_2_out_31), .in_17(kok_2_out_33),
    .in_18(kok_2_out_35), .in_19(kok_2_out_37), .in_20(kok_2_out_39), .in_21(kok_2_out_41),
    .in_22(kok_2_out_43), .out_23(sum_points_2_out_23));
  // Probe on kok_2_out_23
  // Probe on kok_2_out_25
  // Probe on kok_2_out_27
  // Probe on kok_2_out_29
  // Probe on kok_2_out_31
  // Probe on kok_2_out_33
  // Probe on kok_2_out_35
  // Probe on kok_2_out_37
  // Probe on kok_2_out_39
  // Probe on kok_2_out_41
  // Probe on kok_2_out_43
  // Probe on \с0 
  // Probe on \с1 
  // Probe on \с2 
  // Probe on \с3 
  // Probe on \с4 
  Counter counter_6 (.carry(counter_6_carry), .clk(and_7_out));  // open: load, D, count, Q, clr
  tor tor_8 (.in_1(counter_6_carry), .in_2(start_bot), .out_3(tor_8_out_3));
  tt tt_8 (.in_1(tor_8_out_3), .out_2(tt_8_out_2));
  and and_7 (and_7_out, clk, tor_9_out_3);
  tand tand_3 (.in_1(not_17_out), .in_2(clk), .out_3(cIk));
  not not_17 (not_17_out, hoId);
  tor tor_9 (.in_1(tt_8_out_2), .in_2(counter_6_carry), .out_3(tor_9_out_3));
  assign controlled_buffer_5_out = in3 ? 16'h11a6 : 16'bz;  // Controlled_Buffer controlled_buffer_5
  // Probe on {{5{1'b0}}, not_2_out}
  assign controlled_buffer_6_out = not_18_out ? cdm_16_1_p13 : 16'bz;  // Controlled_Buffer controlled_buffer_6
  not not_18 (not_18_out, tand_4_out_3);
  assign controlled_buffer_7_out = not_20_out ? controlled_buffer_6_out : 16'bz;  // Controlled_Buffer controlled_buffer_7
  tand tand_4 (.in_1(cdm_16_1_p10), .in_2(not_20_out), .out_3(tand_4_out_3));
  tor tor_10 (.in_1(in1), .in_2(tand_5_out_3), .out_3(tor_10_out_3));
  tt tt_9 (.in_1(tor_10_out_3), .out_2(tt_9_out_2));
  tand tand_5 (.in_1(not_16_out), .in_2(tick_6_out_2), .out_3(tand_5_out_3));
  and and_8 (and_8_out, clk, tor_13_out_3);
  // Probe on ram_1_data
  assign ram_1_data = counter_2_carry ? 8'he4 : 8'bz;  // Controlled_Buffer controlled_buffer_8
  // Probe on ram_1_data
  // Probe on ram_1_data
  assign ram_1_data = counter_3_carry ? 8'h2a : 8'bz;  // Controlled_Buffer controlled_buffer_9
  assign ram_1_data = counter_4_carry ? 8'h45 : 8'bz;  // Controlled_Buffer controlled_buffer_10
  // Probe on ram_1_data
  Counter #(.width(13), .max('h1669)) counter_7 (
    .carry(counter_7_carry), .clk(and_9_out));  // open: load, D, count, Q, clr
  and and_9 (and_9_out, clk, tor_11_out_3);
  tor tor_11 (.in_1(tt_11_out_2), .in_2(counter_7_carry), .out_3(tor_11_out_3));
  not not_19 (not_19_out, tt_8_out_2);
  tick tick_4 (.in_1(not_19_out), .out_2(tick_4_out_2));
  assign controlled_buffer_5_out = in1 ? 16'h11a2 : 16'bz;  // Controlled_Buffer controlled_buffer_11
  assign controlled_buffer_5_out = in2 ? 16'h11a4 : 16'bz;  // Controlled_Buffer controlled_buffer_12
  assign controlled_buffer_5_out = not_20_out ? cdm_16_1_p12 : 16'bz;  // Controlled_Buffer controlled_buffer_13
  not not_20 (not_20_out, hoId);
  Counter #(.width(3), .max('h7)) counter_8 (.carry(in2), .clk(and_8_out));  // open: load, D, count, Q, clr
  tor tor_12 (.in_1(in2), .in_2(tand_6_out_3), .out_3(tor_12_out_3));
  tt tt_10 (.in_1(tor_12_out_3), .out_2(tt_10_out_2));
  not not_21 (not_21_out, tt_10_out_2);
  tand tand_6 (.in_1(not_21_out), .in_2(tick_6_out_2), .out_3(tand_6_out_3));
  tor tor_13 (.in_1(tt_10_out_2), .in_2(in2), .out_3(tor_13_out_3));
  tor tor_14 (.in_1(counter_7_carry), .in_2(tick_4_out_2), .out_3(tor_14_out_3));
  tt tt_11 (.in_1(tor_14_out_3), .out_2(tt_11_out_2));
  not not_22 (not_22_out, tt_11_out_2);
  tick tick_5 (.in_1(not_22_out), .out_2(tick_5_out_2));
  and and_10 (and_10_out, clk, tor_18_out_3);
  assign bit_extender_1_out = {{15{1'b0}}, e};  // Bit_Extender bit_extender_1
  // AND_Gate and_11 has open pins: in0=cdm_16_1_p10, in1=not_20_out, out=open
  Counter #(.width(4), .max('hf)) counter_9 (.carry(in3), .clk(and_12_out));  // open: load, D, count, Q, clr
  and and_12 (and_12_out, clk, tor_15_out_3);
  tor tor_15 (.in_1(tt_13_out_2), .in_2(in3), .out_3(tor_15_out_3));
  Counter #(.width(3), .max('h7)) counter_10 (
    .carry(counter_10_carry), .clk(and_13_out));  // open: load, D, count, Q, clr
  and and_13 (and_13_out, clk, tor_16_out_3);
  tor tor_16 (.in_1(tt_14_out_2), .in_2(counter_10_carry), .out_3(tor_16_out_3));
  Counter #(.width(3), .max('h7)) counter_11 (
    .carry(counter_11_carry), .clk(and_10_out));  // open: load, D, count, Q, clr
  tor tor_17 (.in_1(counter_11_carry), .in_2(or_4_out), .out_3(tor_17_out_3));
  tt tt_12 (.in_1(tor_17_out_3), .out_2(tt_12_out_2));
  not not_23 (not_23_out, tor_18_out_3);
  tor tor_18 (.in_1(tt_12_out_2), .in_2(counter_11_carry), .out_3(tor_18_out_3));
  assign controlled_buffer_7_out = in1 ? {1'b0, \с4 , \с3 , \с2 , \с1 , \с0 } : 16'bz;  // Controlled_Buffer controlled_buffer_14
  assign controlled_buffer_7_out = in2 ? {{5{1'b0}}, not_2_out} : 16'bz;  // Controlled_Buffer controlled_buffer_15
  assign controlled_buffer_7_out = in3 ? bit_extender_1_out : 16'bz;  // Controlled_Buffer controlled_buffer_16
  // RAM ram_2: pin names not known; wires that end beside it: controlled_buffer_5_out, w, m, clk, controlled_buffer_7_out
  tor tor_19 (.in_1(in3), .in_2(tand_7_out_3), .out_3(tor_19_out_3));
  tt tt_13 (.in_1(tor_19_out_3), .out_2(tt_13_out_2));
  not not_24 (not_24_out, tt_13_out_2);
  tand tand_7 (.in_1(not_24_out), .in_2(tick_6_out_2), .out_3(tand_7_out_3));
  tick tick_6 (.in_1(hoId), .out_2(tick_6_out_2));
  tor tor_20 (.in_1(counter_10_carry), .in_2(tick_5_out_2), .out_3(tor_20_out_3));
  tt tt_14 (.in_1(tor_20_out_3), .out_2(tt_14_out_2));
  Pull_Resistor pull_resistor_1 (.node(pull_resistor_1_node));
  Transistor #(.\type ("n"), .width(16)) transistor_1 (
    .in(cdm_16_1_p2), .out(pull_resistor_1_node), .gate(tt_14_out_2));
  Bit_Extender #(.in_width(16), .out_width(4)) bit_extender_2 (.in(pull_resistor_1_node), .out(bit_extender_2_out));
  tand tand_8 (.in_1(pull_resistor_1_node[15]), .in_2(not_23_out), .out_3(tand_8_out_3));
  Demultiplexer #(.select(4), .disabled(0)) demultiplexer_1 (
    .out0(demultiplexer_1_out0), .out1(demultiplexer_1_out1), .out2(demultiplexer_1_out2),
    .out3(demultiplexer_1_out3), .out4(demultiplexer_1_out4), .out5(demultiplexer_1_out5),
    .out6(demultiplexer_1_out6), .out7(demultiplexer_1_out7), .out8(demultiplexer_1_out8),
    .out9(demultiplexer_1_out9), .out10(demultiplexer_1_out10), .in(1'b1), .sel(bit_extender_2_out),
    .en(tand_8_out_3));  // open: out11, out12, out13, out14, out15
  not not_25 (not_25_out, pull_resistor_1_node[15]);
  tand tand_9 (.in_1(not_25_out), .in_2(pull_resistor_1_node[0]), .out_3(tand_9_out_3));
  tand tand_10 (.in_1(not_25_out), .in_2(pull_resistor_1_node[1]), .out_3(tand_10_out_3));
  tand tand_11 (.in_1(pull_resistor_1_node[15]), .in_2(tick_7_out_2), .out_3(p00o));
  tand tand_12 (.in_1(pull_resistor_1_node[15]), .in_2(tick_8_out_2), .out_3(p01o));
  tick tick_7 (.in_1(demultiplexer_1_out0), .out_2(tick_7_out_2));
  tick tick_8 (.in_1(demultiplexer_1_out1), .out_2(tick_8_out_2));
  tick tick_9 (.in_1(demultiplexer_1_out2), .out_2(tick_9_out_2));
  tick tick_10 (.in_1(demultiplexer_1_out3), .out_2(tick_10_out_2));
  tick tick_11 (.in_1(demultiplexer_1_out4), .out_2(tick_11_out_2));
  tick tick_12 (.in_1(demultiplexer_1_out5), .out_2(tick_12_out_2));
  tick tick_13 (.in_1(demultiplexer_1_out6), .out_2(tick_13_out_2));
  tick tick_14 (.in_1(demultiplexer_1_out7), .out_2(tick_14_out_2));
  tick tick_15 (.in_1(demultiplexer_1_out8), .out_2(tick_15_out_2));
  tick tick_16 (.in_1(demultiplexer_1_out9), .out_2(tick_16_out_2));
  tick tick_17 (.in_1(demultiplexer_1_out10), .out_2(tick_17_out_2));
  tand tand_13 (.in_1(not_26_out), .in_2(nicesr_1_out_3), .out_3(reroll_bot));
  not not_26 (not_26_out, tor_16_out_3);
  niceSR nicesr_1 (.set(tick_18_out_2), .reset(tor_21_out_3), .out_3(nicesr_1_out_3));
  tick tick_18 (.in_1(tor_16_out_3), .out_2(tick_18_out_2));
  tor tor_21 (.in_1(pull_resistor_1_node[15]), .in_2(reroll_bot), .out_3(tor_21_out_3));
  tand tand_14 (.in_1(not_25_out), .in_2(pull_resistor_1_node[2]), .out_3(tand_14_out_3));
  tand tand_15 (.in_1(not_25_out), .in_2(pull_resistor_1_node[3]), .out_3(tand_15_out_3));
  tand tand_16 (.in_1(not_25_out), .in_2(pull_resistor_1_node[4]), .out_3(tand_16_out_3));
  tand tand_17 (.in_1(pull_resistor_1_node[15]), .in_2(tick_9_out_2), .out_3(p02o));
  tand tand_18 (.in_1(pull_resistor_1_node[15]), .in_2(tick_10_out_2), .out_3(p03o));
  tand tand_19 (.in_1(pull_resistor_1_node[15]), .in_2(tick_11_out_2), .out_3(p04o));
  tand tand_20 (.in_1(pull_resistor_1_node[15]), .in_2(tick_12_out_2), .out_3(p05o));
  tt tt_15 (.in_1(reroll_bot), .out_2(tt_15_out_2));
  tick tick_19 (.in_1(tand_9_out_3), .out_2(_21));
  tick tick_20 (.in_1(tand_10_out_3), .out_2(_22));
  tick tick_21 (.in_1(tand_14_out_3), .out_2(_23));
  tick tick_22 (.in_1(tand_15_out_3), .out_2(_24));
  tick tick_23 (.in_1(tand_16_out_3), .out_2(_25));
  tand tand_21 (.in_1(pull_resistor_1_node[15]), .in_2(tick_13_out_2), .out_3(p06o));
  tand tand_22 (.in_1(pull_resistor_1_node[15]), .in_2(tick_14_out_2), .out_3(p07o));
  tand tand_23 (.in_1(pull_resistor_1_node[15]), .in_2(tick_15_out_2), .out_3(p08o));
  tand tand_24 (.in_1(pull_resistor_1_node[15]), .in_2(tick_16_out_2), .out_3(p09o));
  tand tand_25 (.in_1(pull_resistor_1_node[15]), .in_2(tick_17_out_2), .out_3(p10o));
  or or_4 (or_4_out, p00o, p01o, p02o, p03o, p04o, p05o, p06o, p07o, p08o, p09o, p10o);

  // Other names for the same wires on the sheet: p00 = out_6; p01 = out_8; p02 = out_10; p03 = out_12; p04 = out_14;
  //   p05 = out_16; p06 = out_18; p07 = out_20; p08 = out_22; p09 = out_24; p10 = out_26

  // Notes on the sheet:
  //   sum of 1
  //   sum of 2
  //   sum of 3
  //   sum of 4
  //   sum of 5
  //   sum of 6
  //   three same
  //   four same
  //   fullhouse
  //   in a row
  //   all same
endmodule

module D6 (
  input  roll,
  input  [7:0] in_2,
  input  enable,
  output [2:0] out_4
);

  wire select_max6_1_out_8, select_max6_1_out_9, select_max6_1_out_10, select_max6_1_out_11,
       select_max6_1_out_12, select_max6_1_out_13;
  wire [2:0] adder_1_out, adder_2_out, adder_3_out, adder_5_out, multiplexer_1_out, multiplexer_2_out,
       multiplexer_3_out, multiplexer_4_out, multiplexer_5_out, multiplexer_6_out;
  wire [4:0] random_7_out;
  wire [7:0] random_1_out, random_2_out, random_3_out, random_4_out, random_5_out, random_6_out,
       shift_mul_1_out_4, shift_mul_2_out_4, shift_mul_3_out_4, shift_mul_4_out_4, shift_mul_5_out_4,
       shift_mul_6_out_4;

  shift_mul shift_mul_1 (.in_1(in_2), .in_2(random_1_out), .in_3(3'b000), .out_4(shift_mul_1_out_4));
  Random #(.seed(69)) random_1 (.clk(roll), .next(enable), .out(random_1_out), .clr(1'b0));
  shift_mul shift_mul_2 (.in_1(in_2), .in_2(random_2_out), .in_3(3'b001), .out_4(shift_mul_2_out_4));
  Random #(.seed(228)) random_2 (.clk(roll), .next(enable), .out(random_2_out), .clr(1'b0));
  shift_mul shift_mul_3 (.in_1(in_2), .in_2(random_3_out), .in_3(3'b010), .out_4(shift_mul_3_out_4));
  Random #(.seed(1337)) random_3 (.clk(roll), .next(enable), .out(random_3_out), .clr(1'b0));
  Random #(.seed(52)) random_4 (.clk(roll), .next(enable), .out(random_4_out), .clr(1'b0));
  shift_mul shift_mul_4 (.in_1(in_2), .in_2(random_4_out), .in_3(3'b011), .out_4(shift_mul_4_out_4));
  shift_mul shift_mul_5 (.in_1(in_2), .in_2(random_5_out), .in_3(3'b100), .out_4(shift_mul_5_out_4));
  Random #(.seed(42)) random_5 (.clk(roll), .next(enable), .out(random_5_out), .clr(1'b0));
  shift_mul shift_mul_6 (.in_1(in_2), .in_2(random_6_out), .in_3(3'b101), .out_4(shift_mul_6_out_4));
  Random random_6 (.clk(roll), .next(enable), .out(random_6_out), .clr(1'b0));
  Random #(.width(5), .seed(707)) random_7 (.clk(roll), .next(enable), .out(random_7_out));  // open: clr
  select_max6 select_max6_1 (
    .in_1(shift_mul_1_out_4), .in_2(shift_mul_2_out_4), .in_3(shift_mul_3_out_4), .in_4(shift_mul_4_out_4),
    .in_5(shift_mul_5_out_4), .in_6(shift_mul_6_out_4), .downPriority(random_7_out),
    .out_8(select_max6_1_out_8), .out_9(select_max6_1_out_9), .out_10(select_max6_1_out_10),
    .out_11(select_max6_1_out_11), .out_12(select_max6_1_out_12), .out_13(select_max6_1_out_13));
  Multiplexer #(.width(3), .enable("false")) multiplexer_1 (
    .in0(3'b000), .in1(3'b001), .out(multiplexer_1_out), .sel(select_max6_1_out_8));
  Adder #(.width(3)) adder_1 (
    .a(multiplexer_1_out), .b(multiplexer_2_out), .out(adder_1_out), .cin(1'b0));  // open: cout
  Multiplexer #(.width(3), .enable("false")) multiplexer_2 (
    .in0(3'b000), .in1(3'b010), .out(multiplexer_2_out), .sel(select_max6_1_out_9));
  Multiplexer #(.width(3), .enable("false")) multiplexer_3 (
    .in0(3'b000), .in1(3'b011), .out(multiplexer_3_out), .sel(select_max6_1_out_10));
  Adder #(.width(3)) adder_2 (
    .a(multiplexer_3_out), .b(multiplexer_4_out), .out(adder_2_out), .cin(1'b0));  // open: cout
  Multiplexer #(.width(3), .enable("false")) multiplexer_4 (
    .in0(3'b000), .in1(3'b100), .out(multiplexer_4_out), .sel(select_max6_1_out_11));
  Multiplexer #(.width(3), .enable("false")) multiplexer_5 (
    .in0(3'b000), .in1(3'b101), .out(multiplexer_5_out), .sel(select_max6_1_out_12));
  Adder #(.width(3)) adder_3 (
    .a(multiplexer_5_out), .b(multiplexer_6_out), .out(adder_3_out), .cin(1'b0));  // open: cout
  Multiplexer #(.width(3), .enable("false")) multiplexer_6 (
    .in0(3'b000), .in1(3'b110), .out(multiplexer_6_out), .sel(select_max6_1_out_13));
  Adder #(.width(3)) adder_4 (.a(adder_1_out), .b(adder_5_out), .out(out_4), .cin(1'b0));  // open: cout
  Adder #(.width(3)) adder_5 (.a(adder_2_out), .b(adder_3_out), .out(adder_5_out), .cin(1'b0));  // open: cout
endmodule

module select_max6 (
  input  [7:0] in_1,
  input  [7:0] in_2,
  input  [7:0] in_3,
  input  [7:0] in_4,
  input  [7:0] in_5,
  input  [7:0] in_6,
  input  [4:0] downPriority,
  output out_8,
  output out_9,
  output out_10,
  output out_11,
  output out_12,
  output out_13
);

  wire comparator_1_eq, comparator_2_eq, comparator_3_eq, comparator_4_eq, comparator_5_eq, comparator_6_eq;
  wire [7:0] select_max2_1_out_3, select_max2_2_out_3, select_max2_3_out_3, select_max2_4_out_3,
       select_max2_5_out_3;

  select_max2 select_max2_1 (.in_1(in_1), .in_2(in_2), .out_3(select_max2_1_out_3));
  select_max2 select_max2_2 (.in_1(select_max2_1_out_3), .in_2(select_max2_3_out_3), .out_3(select_max2_2_out_3));
  select_max2 select_max2_3 (.in_1(in_3), .in_2(in_4), .out_3(select_max2_3_out_3));
  select_max2 select_max2_4 (.in_1(in_5), .in_2(in_6), .out_3(select_max2_4_out_3));
  select_max2 select_max2_5 (.in_1(select_max2_2_out_3), .in_2(select_max2_4_out_3), .out_3(select_max2_5_out_3));
  Comparator #(.mode("unsigned")) comparator_1 (
    .a(in_1), .b(select_max2_5_out_3), .eq(comparator_1_eq));  // open: gt, lt
  Comparator #(.mode("unsigned")) comparator_2 (
    .a(in_2), .b(select_max2_5_out_3), .eq(comparator_2_eq));  // open: gt, lt
  Comparator #(.mode("unsigned")) comparator_3 (
    .a(in_3), .b(select_max2_5_out_3), .eq(comparator_3_eq));  // open: gt, lt
  Comparator #(.mode("unsigned")) comparator_4 (
    .a(in_4), .b(select_max2_5_out_3), .eq(comparator_4_eq));  // open: gt, lt
  Comparator #(.mode("unsigned")) comparator_5 (
    .a(in_5), .b(select_max2_5_out_3), .eq(comparator_5_eq));  // open: gt, lt
  Comparator #(.mode("unsigned")) comparator_6 (
    .a(in_6), .b(select_max2_5_out_3), .eq(comparator_6_eq));  // open: gt, lt
  priorityze_better priorityze_better_1 (
    .in_1(comparator_1_eq), .in_2(comparator_2_eq), .in_3(comparator_3_eq), .in_4(comparator_4_eq),
    .in_5(comparator_5_eq), .in_6(comparator_6_eq), .in_7(downPriority), .out_8(out_8), .out_9(out_9),
    .out_10(out_10), .out_11(out_11), .out_12(out_12), .out_13(out_13));
endmodule

module select_max2 (
  input  [7:0] in_1,
  input  [7:0] in_2,
  output [7:0] out_3
);

  wire comparator_1_eq, comparator_1_lt, or_1_out;

  Comparator #(.mode("unsigned")) comparator_1 (
    .a(in_1), .b(in_2), .eq(comparator_1_eq), .lt(comparator_1_lt));  // open: gt
  Multiplexer #(.width(8), .enable("false")) multiplexer_1 (.in0(in_1), .in1(in_2), .out(out_3), .sel(or_1_out));
  or or_1 (or_1_out, comparator_1_eq, comparator_1_lt);
endmodule

module priorityze6 (
  input  in_1,
  input  in_2,
  input  in_3,
  input  in_4,
  input  in_5,
  input  in_6,
  input  priorityzeDown,
  output out_8,
  output out_9,
  output out_10,
  output out_11,
  output out_12,
  output out_13
);

  wire transistor_1_out, transistor_2_out, transistor_3_out, transistor_4_out, transistor_5_out,
       transistor_6_out, transistor_7_out, transistor_8_out, transistor_9_out, transistor_10_out,
       transistor_11_out, transistor_12_out, transistor_13_out, transistor_14_out, transistor_15_out,
       transistor_16_out, transistor_17_out, transistor_18_out, transistor_19_out, transistor_20_out;
  wire [4:0] pull_resistor_10_node;
  wire [5:1] transistor_21_out;

  Transistor transistor_1 (.in(in_5), .out(transistor_1_out), .gate(in_4));
  Transistor transistor_2 (.in(transistor_3_out), .out(transistor_2_out), .gate(in_4));
  Transistor transistor_3 (.in(in_6), .out(transistor_3_out), .gate(in_5));
  Transistor transistor_4 (.in(in_2), .out(transistor_4_out), .gate(in_3));
  Transistor transistor_5 (.in(transistor_6_out), .out(transistor_5_out), .gate(in_3));
  Transistor transistor_6 (.in(in_1), .out(transistor_6_out), .gate(in_2));
  Transistor transistor_7 (.in(in_3), .out(transistor_7_out), .gate(in_2));
  Transistor transistor_8 (.in(in_4), .out(transistor_8_out), .gate(in_3));
  Transistor transistor_9 (.in(transistor_8_out), .out(transistor_9_out), .gate(in_2));
  Transistor transistor_10 (.in(transistor_11_out), .out(transistor_10_out), .gate(in_2));
  Transistor transistor_11 (.in(transistor_1_out), .out(transistor_11_out), .gate(in_3));
  Transistor transistor_12 (.in(transistor_13_out), .out(transistor_12_out), .gate(in_2));
  Transistor transistor_13 (.in(transistor_2_out), .out(transistor_13_out), .gate(in_3));
  Transistor transistor_14 (.in(in_4), .out(transistor_14_out), .gate(in_5));
  Transistor transistor_15 (.in(transistor_16_out), .out(transistor_15_out), .gate(in_5));
  Transistor transistor_16 (.in(in_3), .out(transistor_16_out), .gate(in_4));
  Transistor transistor_17 (.in(transistor_18_out), .out(transistor_17_out), .gate(in_5));
  Transistor transistor_18 (.in(transistor_4_out), .out(transistor_18_out), .gate(in_4));
  Transistor transistor_19 (.in(transistor_5_out), .out(transistor_19_out), .gate(in_4));
  Transistor transistor_20 (.in(transistor_19_out), .out(transistor_20_out), .gate(in_5));
  Transistor transistor_21 (.in(in_2), .out(transistor_21_out[1]), .gate(in_1));
  Pull_Resistor pull_resistor_1 (.node(transistor_21_out[1]));
  Pull_Resistor pull_resistor_2 (.node(transistor_21_out[2]));
  Transistor transistor_22 (.in(transistor_7_out), .out(transistor_21_out[2]), .gate(in_1));
  Transistor transistor_23 (.in(transistor_9_out), .out(transistor_21_out[3]), .gate(in_1));
  Pull_Resistor pull_resistor_3 (.node(transistor_21_out[3]));
  Pull_Resistor pull_resistor_4 (.node(transistor_21_out[4]));
  Transistor transistor_24 (.in(transistor_10_out), .out(transistor_21_out[4]), .gate(in_1));
  Pull_Resistor pull_resistor_5 (.node(transistor_21_out[5]));
  Transistor transistor_25 (.in(transistor_12_out), .out(transistor_21_out[5]), .gate(in_1));
  Pull_Resistor pull_resistor_6 (.node(pull_resistor_10_node[4]));
  Transistor transistor_26 (.in(in_5), .out(pull_resistor_10_node[4]), .gate(in_6));
  Transistor transistor_27 (.in(transistor_14_out), .out(pull_resistor_10_node[3]), .gate(in_6));
  Pull_Resistor pull_resistor_7 (.node(pull_resistor_10_node[3]));
  Pull_Resistor pull_resistor_8 (.node(pull_resistor_10_node[2]));
  Transistor transistor_28 (.in(transistor_15_out), .out(pull_resistor_10_node[2]), .gate(in_6));
  Pull_Resistor pull_resistor_9 (.node(pull_resistor_10_node[1]));
  Transistor transistor_29 (.in(transistor_17_out), .out(pull_resistor_10_node[1]), .gate(in_6));
  Pull_Resistor pull_resistor_10 (.node(pull_resistor_10_node[0]));
  Transistor transistor_30 (.in(transistor_20_out), .out(pull_resistor_10_node[0]), .gate(in_6));
  Multiplexer #(.width(6), .enable("false")) multiplexer_1 (
    .in0({transistor_21_out, in_1}), .in1({in_6, pull_resistor_10_node}),
    .out({out_13, out_12, out_11, out_10, out_9, out_8}), .sel(priorityzeDown));
endmodule

module shift_mul (
  input  [7:0] in_1,
  input  [7:0] in_2,
  input  [2:0] in_3,
  output [7:0] out_4
);

  wire [7:0] shifter_1_out;

  Shifter #(.shift("rl")) shifter_1 (.in(in_1), .\dist (in_3), .out(shifter_1_out));
  Multiplier multiplier_1 (.a(shifter_1_out), .b(in_2), .out(out_4), .cin({8{1'b0}}));  // open: cout
endmodule

module player_panel (
  input  Roll,
  input  in_2,
  input  in_3,
  input  in_4,
  input  in_5,
  input  in_6,
  input  Enable,
  input  Enable_cubes,
  output [2:0] out_9,
  output [2:0] out_10,
  output [2:0] out_11,
  output [2:0] out_12,
  output [2:0] out_13
);

  wire and_1_out, button_1_out, not_1_out;
  wire [2:0] d6_better_1_out_4, d6_better_2_out_4, d6_better_3_out_4, d6_better_4_out_4, d6_better_5_out_4;
  wire [7:0] random_1_out, random_2_out, random_3_out, random_4_out, random_5_out;

  Button button_1 (.out(button_1_out));
  Random random_1 (.clk(and_1_out), .next(in_2), .out(random_1_out), .clr(button_1_out));
  Random #(.seed(69)) random_2 (.clk(and_1_out), .next(in_3), .out(random_2_out), .clr(button_1_out));
  Random #(.seed(420)) random_3 (.clk(and_1_out), .next(in_4), .out(random_3_out), .clr(button_1_out));
  Random #(.seed(1337)) random_4 (.clk(and_1_out), .next(in_5), .out(random_4_out), .clr(button_1_out));
  Random #(.seed(999)) random_5 (.clk(and_1_out), .next(in_6), .out(random_5_out), .clr(button_1_out));
  and and_1 (and_1_out, Enable, Roll);
  D6_better d6_better_1 (.roll(and_1_out), .in_3(random_1_out), .enable(in_2), .out_4(d6_better_1_out_4));
  D6_better d6_better_2 (.roll(and_1_out), .in_3(random_2_out), .enable(in_3), .out_4(d6_better_2_out_4));
  D6_better d6_better_3 (.roll(and_1_out), .in_3(random_3_out), .enable(in_4), .out_4(d6_better_3_out_4));
  D6_better d6_better_4 (.roll(and_1_out), .in_3(random_4_out), .enable(in_5), .out_4(d6_better_4_out_4));
  D6_better d6_better_5 (.roll(and_1_out), .in_3(random_5_out), .enable(in_6), .out_4(d6_better_5_out_4));
  // Probe on d6_better_1_out_4
  Multiplexer #(.width(3), .enable("false")) multiplexer_1 (
    .in0(d6_better_1_out_4), .in1(3'b000), .out(out_9), .sel(not_1_out));
  // Probe on d6_better_2_out_4
  Multiplexer #(.width(3), .enable("false")) multiplexer_2 (
    .in0(d6_better_2_out_4), .in1(3'b000), .out(out_10), .sel(not_1_out));
  // Probe on d6_better_3_out_4
  Multiplexer #(.width(3), .enable("false")) multiplexer_3 (
    .in0(d6_better_3_out_4), .in1(3'b000), .out(out_11), .sel(not_1_out));
  // Probe on d6_better_4_out_4
  Multiplexer #(.width(3), .enable("false")) multiplexer_4 (
    .in0(d6_better_4_out_4), .in1(3'b000), .out(out_12), .sel(not_1_out));
  // Probe on d6_better_5_out_4
  Multiplexer #(.width(3), .enable("false")) multiplexer_5 (
    .in0(d6_better_5_out_4), .in1(3'b000), .out(out_13), .sel(not_1_out));
  not not_1 (not_1_out, Enable_cubes);
endmodule

module detect_n (
  input  [2:0] in_1,
  input  [2:0] in_2,
  input  [2:0] in_3,
  input  [2:0] in_4,
  input  [2:0] in_5,
  input  [2:0] in_6,
  output [7:0] out_7
);

  wire [3:0] bitadder_1_out;
  wire [7:0] comparator_1_eq;

  Comparator #(.width(3)) comparator_1 (.a(in_1), .b(in_6), .eq(comparator_1_eq[0]));  // open: gt, lt
  Comparator #(.width(3)) comparator_2 (.a(in_6), .b(in_2), .eq(comparator_1_eq[1]));  // open: gt, lt
  Comparator #(.width(3)) comparator_3 (.a(in_6), .b(in_3), .eq(comparator_1_eq[4]));  // open: gt, lt
  Comparator #(.width(3)) comparator_4 (.a(in_4), .b(in_6), .eq(comparator_1_eq[5]));  // open: gt, lt
  Comparator #(.width(3)) comparator_5 (.a(in_6), .b(in_5), .eq(comparator_1_eq[7]));  // open: gt, lt
  BitAdder bitadder_1 (
    .in0({comparator_1_eq[7], 1'b0, comparator_1_eq[5:4], 2'b00, comparator_1_eq[1:0]}), .out(bitadder_1_out));
  assign out_7 = {{4{1'b0}}, bitadder_1_out};  // Bit_Extender bit_extender_1
endmodule

module has_n_same (
  input  [2:0] in_1,
  input  [2:0] in_2,
  input  [2:0] in_3,
  input  [2:0] in_4,
  input  [2:0] in_5,
  input  [7:0] in_6,
  input  in_7,
  output out_8
);

  wire and_1_out, and_2_out, and_3_out, and_4_out, and_5_out, and_6_out, comparator_1_eq, comparator_1_gt,
       comparator_2_eq, comparator_2_gt, comparator_3_eq, comparator_3_gt, comparator_4_eq, comparator_4_gt,
       comparator_5_eq, comparator_5_gt, comparator_6_eq, comparator_6_gt, or_1_out, or_2_out, or_3_out,
       or_4_out, or_5_out, or_6_out;
  wire [7:0] detect_n_1_out_7, detect_n_2_out_7, detect_n_3_out_7, detect_n_4_out_7, detect_n_5_out_7,
       detect_n_6_out_7;

  detect_n detect_n_1 (
    .in_1(in_1), .in_2(in_2), .in_3(in_3), .in_4(in_4), .in_5(in_5), .in_6(3'b001), .out_7(detect_n_1_out_7));
  detect_n detect_n_2 (
    .in_1(in_1), .in_2(in_2), .in_3(in_3), .in_4(in_4), .in_5(in_5), .in_6(3'b010), .out_7(detect_n_2_out_7));
  detect_n detect_n_3 (
    .in_1(in_1), .in_2(in_2), .in_3(in_3), .in_4(in_4), .in_5(in_5), .in_6(3'b011), .out_7(detect_n_3_out_7));
  detect_n detect_n_4 (
    .in_1(in_1), .in_2(in_2), .in_3(in_3), .in_4(in_4), .in_5(in_5), .in_6(3'b100), .out_7(detect_n_4_out_7));
  detect_n detect_n_5 (
    .in_1(in_1), .in_2(in_2), .in_3(in_3), .in_4(in_4), .in_5(in_5), .in_6(3'b101), .out_7(detect_n_5_out_7));
  detect_n detect_n_6 (
    .in_1(in_1), .in_2(in_2), .in_3(in_3), .in_4(in_4), .in_5(in_5), .in_6(3'b110), .out_7(detect_n_6_out_7));
  Comparator comparator_1 (.a(detect_n_1_out_7), .b(in_6), .gt(comparator_1_gt), .eq(comparator_1_eq));  // open: lt
  Comparator comparator_2 (.a(detect_n_2_out_7), .b(in_6), .gt(comparator_2_gt), .eq(comparator_2_eq));  // open: lt
  Comparator comparator_3 (.a(detect_n_3_out_7), .b(in_6), .gt(comparator_3_gt), .eq(comparator_3_eq));  // open: lt
  Comparator comparator_4 (.a(detect_n_4_out_7), .b(in_6), .gt(comparator_4_gt), .eq(comparator_4_eq));  // open: lt
  Comparator comparator_5 (.a(detect_n_5_out_7), .b(in_6), .gt(comparator_5_gt), .eq(comparator_5_eq));  // open: lt
  Comparator comparator_6 (.a(detect_n_6_out_7), .b(in_6), .gt(comparator_6_gt), .eq(comparator_6_eq));  // open: lt
  and and_1 (and_1_out, in_7, comparator_1_gt);
  or or_1 (or_1_out, and_1_out, comparator_1_eq);
  and and_2 (and_2_out, in_7, comparator_2_gt);
  or or_2 (or_2_out, and_2_out, comparator_2_eq);
  and and_3 (and_3_out, in_7, comparator_3_gt);
  or or_3 (or_3_out, and_3_out, comparator_3_eq);
  and and_4 (and_4_out, in_7, comparator_4_gt);
  or or_4 (or_4_out, and_4_out, comparator_4_eq);
  and and_5 (and_5_out, in_7, comparator_5_gt);
  or or_5 (or_5_out, and_5_out, comparator_5_eq);
  and and_6 (and_6_out, in_7, comparator_6_gt);
  or or_6 (or_6_out, and_6_out, comparator_6_eq);
  or or_7 (out_8, or_1_out, or_2_out, or_3_out, or_4_out, or_5_out, or_6_out);
endmodule

module detect_3_same (
  input  [2:0] in_1,
  input  [2:0] in_2,
  input  [2:0] in_3,
  input  [2:0] in_4,
  input  [2:0] in_5,
  output out_6
);

  has_n_same has_n_same_1 (
    .in_1(in_1), .in_2(in_2), .in_3(in_3), .in_4(in_4), .in_5(in_5), .in_6(8'h3), .in_7(1'b1), .out_8(out_6));
endmodule

module detect_4_same (
  input  [2:0] in_1,
  input  [2:0] in_2,
  input  [2:0] in_3,
  input  [2:0] in_4,
  input  [2:0] in_5,
  output out_6
);

  has_n_same has_n_same_1 (
    .in_1(in_1), .in_2(in_2), .in_3(in_3), .in_4(in_4), .in_5(in_5), .in_6(8'h4), .in_7(1'b1), .out_8(out_6));
endmodule

module detect_5_same (
  input  [2:0] in_1,
  input  [2:0] in_2,
  input  [2:0] in_3,
  input  [2:0] in_4,
  input  [2:0] in_5,
  output out_6
);

  has_n_same has_n_same_1 (
    .in_1(in_1), .in_2(in_2), .in_3(in_3), .in_4(in_4), .in_5(in_5), .in_6(8'h5), .in_7(1'b1), .out_8(out_6));
endmodule

module detect_fullhouse (
  input  [2:0] in_1,
  input  [2:0] in_2,
  input  [2:0] in_3,
  input  [2:0] in_4,
  input  [2:0] in_5,
  output out_6
);

  wire has_n_same_1_out_8, has_n_same_2_out_8, has_n_same_3_out_8, not_1_out;

  has_n_same has_n_same_1 (
    .in_1(in_1), .in_2(in_2), .in_3(in_3), .in_4(in_4), .in_5(in_5), .in_6(8'h2), .in_7(1'b0),
    .out_8(has_n_same_1_out_8));
  has_n_same has_n_same_2 (
    .in_1(in_1), .in_2(in_2), .in_3(in_3), .in_4(in_4), .in_5(in_5), .in_6(8'h3), .in_7(1'b0),
    .out_8(has_n_same_2_out_8));
  has_n_same has_n_same_3 (
    .in_1(in_1), .in_2(in_2), .in_3(in_3), .in_4(in_4), .in_5(in_5), .in_6(8'h5), .in_7(1'b0),
    .out_8(has_n_same_3_out_8));
  not not_1 (not_1_out, has_n_same_3_out_8);
  and and_1 (out_6, has_n_same_1_out_8, has_n_same_2_out_8, not_1_out);
endmodule

module detect_straight (
  input  [2:0] in_1,
  input  [2:0] in_2,
  input  [2:0] in_3,
  input  [2:0] in_4,
  input  [2:0] in_5,
  output out_6
);

  wire comparator_1_eq, comparator_2_eq, has_n_same_1_out_8, not_1_out, xor_1_out;
  wire [7:0] detect_n_1_out_7, detect_n_2_out_7;

  detect_n detect_n_1 (
    .in_1(in_1), .in_2(in_2), .in_3(in_3), .in_4(in_4), .in_5(in_5), .in_6(3'b110), .out_7(detect_n_1_out_7));
  Comparator comparator_1 (.a(detect_n_1_out_7), .b({8{1'b0}}), .eq(comparator_1_eq));  // open: gt, lt
  detect_n detect_n_2 (
    .in_1(in_1), .in_2(in_2), .in_3(in_3), .in_4(in_4), .in_5(in_5), .in_6(3'b001), .out_7(detect_n_2_out_7));
  Comparator comparator_2 (.a(detect_n_2_out_7), .b({8{1'b0}}), .eq(comparator_2_eq));  // open: gt, lt
  not not_1 (not_1_out, has_n_same_1_out_8);
  has_n_same has_n_same_1 (
    .in_1(in_1), .in_2(in_2), .in_3(in_3), .in_4(in_4), .in_5(in_5), .in_6(8'h2), .in_7(1'b1),
    .out_8(has_n_same_1_out_8));
  xor xor_1 (xor_1_out, comparator_1_eq, comparator_2_eq);
  and and_1 (out_6, xor_1_out, not_1_out);
endmodule

module sum5 (
  input  [2:0] in_1,
  input  [2:0] in_2,
  input  [2:0] in_3,
  input  [2:0] in_4,
  input  [2:0] in_5,
  output [7:0] out_6
);

  wire [7:0] adder_1_out, adder_2_out, adder_3_out, bit_extender_1_out, bit_extender_2_out,
       bit_extender_3_out, bit_extender_4_out, bit_extender_5_out;

  assign bit_extender_1_out = {{5{1'b0}}, in_1};  // Bit_Extender bit_extender_1
  assign bit_extender_2_out = {{5{1'b0}}, in_2};  // Bit_Extender bit_extender_2
  assign bit_extender_3_out = {{5{1'b0}}, in_3};  // Bit_Extender bit_extender_3
  assign bit_extender_4_out = {{5{1'b0}}, in_4};  // Bit_Extender bit_extender_4
  assign bit_extender_5_out = {{5{1'b0}}, in_5};  // Bit_Extender bit_extender_5
  Adder adder_1 (.a(bit_extender_1_out), .b(bit_extender_2_out), .out(adder_1_out), .cin(1'b0));  // open: cout
  Adder adder_2 (.a(bit_extender_3_out), .b(bit_extender_4_out), .out(adder_2_out), .cin(1'b0));  // open: cout
  Adder adder_3 (.a(adder_1_out), .b(adder_2_out), .out(adder_3_out), .cin(1'b0));  // open: cout
  Adder adder_4 (.a(adder_3_out), .b(bit_extender_5_out), .out(out_6), .cin(1'b0));  // open: cout
endmodule

module priorityze_better (
  input  in_1,
  input  in_2,
  input  in_3,
  input  in_4,
  input  in_5,
  input  in_6,
  input  [4:0] in_7,
  output out_8,
  output out_9,
  output out_10,
  output out_11,
  output out_12,
  output out_13
);

  wire and_1_out, and_2_out, and_3_out, and_4_out;
  wire [0:0] pull_resistor_6_node, transistor_2_out, transistor_4_out;
  wire [1:0] multiplexer_1_out, multiplexer_2_out, multiplexer_3_out, multiplexer_4_out, multiplexer_5_out,
       or_1_out, or_4_out, transistor_8_out, transistor_10_out;
  wire [1:1] pull_resistor_3_node, pull_resistor_5_node, transistor_1_out;

  Transistor transistor_1 (.in(in_2), .out(transistor_1_out[1]), .gate(in_1));
  Pull_Resistor pull_resistor_1 (.node(transistor_1_out[1]));
  Transistor transistor_2 (.in(in_1), .out(transistor_2_out[0]), .gate(in_2));
  Pull_Resistor pull_resistor_2 (.node(transistor_2_out[0]));
  Pull_Resistor pull_resistor_3 (.node(pull_resistor_3_node[1]));
  Transistor transistor_3 (.in(in_4), .out(pull_resistor_3_node[1]), .gate(in_3));
  Transistor transistor_4 (.in(in_3), .out(transistor_4_out[0]), .gate(in_4));
  Pull_Resistor pull_resistor_4 (.node(transistor_4_out[0]));
  Pull_Resistor pull_resistor_5 (.node(pull_resistor_5_node[1]));
  Transistor transistor_5 (.in(in_6), .out(pull_resistor_5_node[1]), .gate(in_5));
  Pull_Resistor pull_resistor_6 (.node(pull_resistor_6_node[0]));
  Transistor transistor_6 (.in(in_5), .out(pull_resistor_6_node[0]), .gate(in_6));
  Multiplexer #(.width(2), .enable("false")) multiplexer_1 (
    .in0({transistor_1_out[1], in_1}), .in1({in_2, transistor_2_out[0]}), .out(multiplexer_1_out),
    .sel(in_7[4]));
  Multiplexer #(.width(2), .enable("false")) multiplexer_2 (
    .in0({pull_resistor_3_node[1], in_3}), .in1({in_4, transistor_4_out[0]}), .out(multiplexer_2_out),
    .sel(in_7[3]));
  Multiplexer #(.width(2), .enable("false")) multiplexer_3 (
    .in0({pull_resistor_5_node[1], in_5}), .in1({in_6, pull_resistor_6_node[0]}), .out(multiplexer_3_out),
    .sel(in_7[2]));
  or or_1 (or_1_out[0], multiplexer_1_out[0], multiplexer_1_out[1]);
  or or_2 (transistor_8_out[1], multiplexer_2_out[0], multiplexer_2_out[1]);
  Pull_Resistor pull_resistor_7 (.node(or_1_out[1]));
  Transistor transistor_7 (.in(transistor_8_out[1]), .out(or_1_out[1]), .gate(or_1_out[0]));
  Transistor transistor_8 (.in(or_1_out[0]), .out(transistor_8_out[0]), .gate(transistor_8_out[1]));
  Pull_Resistor pull_resistor_8 (.node(transistor_8_out[0]));
  or or_3 (transistor_10_out[1], multiplexer_3_out[0], multiplexer_3_out[1]);
  Multiplexer #(.width(2), .enable("false")) multiplexer_4 (
    .in0(or_1_out), .in1(transistor_8_out), .out(multiplexer_4_out), .sel(in_7[1]));
  and and_1 (and_1_out, multiplexer_1_out[0], multiplexer_4_out[0]);
  and and_2 (and_2_out, multiplexer_1_out[1], multiplexer_4_out[0]);
  or or_4 (or_4_out[0], and_1_out, and_2_out, and_3_out, and_4_out);
  and and_3 (and_3_out, multiplexer_4_out[1], multiplexer_2_out[0]);
  and and_4 (and_4_out, multiplexer_4_out[1], multiplexer_2_out[1]);
  Transistor transistor_9 (.in(transistor_10_out[1]), .out(or_4_out[1]), .gate(or_4_out[0]));
  Pull_Resistor pull_resistor_9 (.node(or_4_out[1]));
  Transistor transistor_10 (.in(or_4_out[0]), .out(transistor_10_out[0]), .gate(transistor_10_out[1]));
  Pull_Resistor pull_resistor_10 (.node(transistor_10_out[0]));
  Multiplexer #(.width(2), .enable("false")) multiplexer_5 (
    .in0(or_4_out), .in1(transistor_10_out), .out(multiplexer_5_out), .sel(in_7[0]));
  and and_5 (out_8, and_1_out, multiplexer_5_out[0]);
  and and_6 (out_9, and_2_out, multiplexer_5_out[0]);
  and and_7 (out_10, and_3_out, multiplexer_5_out[0]);
  and and_8 (out_11, and_4_out, multiplexer_5_out[0]);
  and and_9 (out_12, multiplexer_5_out[1], multiplexer_3_out[0]);
  and and_10 (out_13, multiplexer_5_out[1], multiplexer_3_out[0]);

  // Other names for the same wires on the sheet: _5 = in_7[0]; _4 = in_7[1]; _3 = in_7[2]; _2 = in_7[3]; _1 = in_7[4]
endmodule

module priorityze2 (
  input  in_1,
  input  in_2,
  input  in_3,
  output out_4,
  output out_5
);

  wire [0:0] transistor_2_out;
  wire [1:1] transistor_1_out;

  Transistor transistor_1 (.in(in_2), .out(transistor_1_out[1]), .gate(in_1));
  Pull_Resistor pull_resistor_1 (.node(transistor_1_out[1]));
  Transistor transistor_2 (.in(in_1), .out(transistor_2_out[0]), .gate(in_2));
  Pull_Resistor pull_resistor_2 (.node(transistor_2_out[0]));
  Multiplexer #(.width(2), .enable("false")) multiplexer_1 (
    .in0({transistor_1_out[1], in_1}), .in1({in_2, transistor_2_out[0]}), .out({out_5, out_4}), .sel(in_3));
endmodule

module tand (
  input  in_1,
  input  in_2,
  output out_3
);

  and and_1 (out_3, in_1, in_2);
endmodule

module manage_cubes (
  input  [2:0] in_1,
  input  [2:0] in_2,
  input  [2:0] in_3,
  input  [2:0] in_4,
  input  [2:0] in_5,
  input  enable,
  output [7:0] out_7,
  output [7:0] out_8,
  output [7:0] out_9,
  output [7:0] out_10,
  output [7:0] out_11,
  output [7:0] out_12,
  output [7:0] out_13,
  output [7:0] out_14,
  output [7:0] out_15,
  output [7:0] out_16,
  output [7:0] out_17
);

  wire detect_3_same_1_out_6, detect_4_same_1_out_6, detect_5_same_1_out_6, detect_fullhouse_1_out_6,
       detect_straight_1_out_6, tand_1_out_3, tand_2_out_3, tand_3_out_3, tand_4_out_3, tand_5_out_3;
  wire [7:0] detect_n_1_out_7, detect_n_2_out_7, detect_n_3_out_7, detect_n_4_out_7, detect_n_5_out_7,
       detect_n_6_out_7, multiplier_1_out, multiplier_2_out, multiplier_3_out, multiplier_4_out,
       multiplier_5_out, multiplier_6_out, sum5_1_out_6;

  detect_n detect_n_1 (
    .in_1(in_1), .in_2(in_2), .in_3(in_3), .in_4(in_4), .in_5(in_5), .in_6(3'b001), .out_7(detect_n_1_out_7));
  Multiplier multiplier_1 (.a(detect_n_1_out_7), .b(8'h1), .out(multiplier_1_out));  // open: cin, cout
  detect_n detect_n_2 (
    .in_1(in_1), .in_2(in_2), .in_3(in_3), .in_4(in_4), .in_5(in_5), .in_6(3'b010), .out_7(detect_n_2_out_7));
  Multiplier multiplier_2 (.a(detect_n_2_out_7), .b(8'h2), .out(multiplier_2_out));  // open: cin, cout
  detect_n detect_n_3 (
    .in_1(in_1), .in_2(in_2), .in_3(in_3), .in_4(in_4), .in_5(in_5), .in_6(3'b011), .out_7(detect_n_3_out_7));
  Multiplier multiplier_3 (.a(detect_n_3_out_7), .b(8'h3), .out(multiplier_3_out));  // open: cin, cout
  detect_n detect_n_4 (
    .in_1(in_1), .in_2(in_2), .in_3(in_3), .in_4(in_4), .in_5(in_5), .in_6(3'b100), .out_7(detect_n_4_out_7));
  Multiplier multiplier_4 (.a(detect_n_4_out_7), .b(8'h4), .out(multiplier_4_out));  // open: cin, cout
  detect_n detect_n_5 (
    .in_1(in_1), .in_2(in_2), .in_3(in_3), .in_4(in_4), .in_5(in_5), .in_6(3'b101), .out_7(detect_n_5_out_7));
  Multiplier multiplier_5 (.a(detect_n_5_out_7), .b(8'h5), .out(multiplier_5_out));  // open: cin, cout
  detect_n detect_n_6 (
    .in_1(in_1), .in_2(in_2), .in_3(in_3), .in_4(in_4), .in_5(in_5), .in_6(3'b110), .out_7(detect_n_6_out_7));
  Multiplier multiplier_6 (.a(detect_n_6_out_7), .b(8'h6), .out(multiplier_6_out));  // open: cin, cout
  detect_3_same detect_3_same_1 (
    .in_1(in_1), .in_2(in_2), .in_3(in_3), .in_4(in_4), .in_5(in_5), .out_6(detect_3_same_1_out_6));
  tand tand_1 (.in_1(detect_3_same_1_out_6), .in_2(enable), .out_3(tand_1_out_3));
  detect_4_same detect_4_same_1 (
    .in_1(in_1), .in_2(in_2), .in_3(in_3), .in_4(in_4), .in_5(in_5), .out_6(detect_4_same_1_out_6));
  tand tand_2 (.in_1(detect_4_same_1_out_6), .in_2(enable), .out_3(tand_2_out_3));
  detect_fullhouse detect_fullhouse_1 (
    .in_1(in_1), .in_2(in_2), .in_3(in_3), .in_4(in_4), .in_5(in_5), .out_6(detect_fullhouse_1_out_6));
  tand tand_3 (.in_1(detect_fullhouse_1_out_6), .in_2(enable), .out_3(tand_3_out_3));
  detect_straight detect_straight_1 (
    .in_1(in_1), .in_2(in_2), .in_3(in_3), .in_4(in_4), .in_5(in_5), .out_6(detect_straight_1_out_6));
  tand tand_4 (.in_1(detect_straight_1_out_6), .in_2(enable), .out_3(tand_4_out_3));
  detect_5_same detect_5_same_1 (
    .in_1(in_1), .in_2(in_2), .in_3(in_3), .in_4(in_4), .in_5(in_5), .out_6(detect_5_same_1_out_6));
  tand tand_5 (.in_1(detect_5_same_1_out_6), .in_2(enable), .out_3(tand_5_out_3));
  sum5 sum5_1 (.in_1(in_1), .in_2(in_2), .in_3(in_3), .in_4(in_4), .in_5(in_5), .out_6(sum5_1_out_6));
  Multiplexer #(.width(8), .enable("false")) multiplexer_1 (
    .in0({8{1'b0}}), .in1(multiplier_1_out), .out(out_7), .sel(enable));
  Multiplexer #(.width(8), .enable("false")) multiplexer_2 (
    .in0({8{1'b0}}), .in1(multiplier_2_out), .out(out_8), .sel(enable));
  Multiplexer #(.width(8), .enable("false")) multiplexer_3 (
    .in0({8{1'b0}}), .in1(multiplier_3_out), .out(out_9), .sel(enable));
  Multiplexer #(.width(8), .enable("false")) multiplexer_4 (
    .in0({8{1'b0}}), .in1(multiplier_4_out), .out(out_10), .sel(enable));
  Multiplexer #(.width(8), .enable("false")) multiplexer_5 (
    .in0({8{1'b0}}), .in1(multiplier_5_out), .out(out_11), .sel(enable));
  Multiplexer #(.width(8), .enable("false")) multiplexer_6 (
    .in0({8{1'b0}}), .in1(multiplier_6_out), .out(out_12), .sel(enable));
  Multiplexer #(.width(8), .enable("false")) multiplexer_7 (
    .in0({8{1'b0}}), .in1(sum5_1_out_6), .out(out_13), .sel(tand_1_out_3));
  Multiplexer #(.width(8), .enable("false")) multiplexer_8 (
    .in0({8{1'b0}}), .in1(sum5_1_out_6), .out(out_14), .sel(tand_2_out_3));
  Multiplexer #(.width(8), .enable("false")) multiplexer_9 (
    .in0({8{1'b0}}), .in1(8'h19), .out(out_15), .sel(tand_3_out_3));
  Multiplexer #(.width(8), .enable("false")) multiplexer_10 (
    .in0({8{1'b0}}), .in1(8'h28), .out(out_16), .sel(tand_4_out_3));
  Multiplexer #(.width(8), .enable("false")) multiplexer_11 (
    .in0({8{1'b0}}), .in1(8'h32), .out(out_17), .sel(tand_5_out_3));
endmodule

module niceSR (
  input  set,
  input  reset,
  output out_3
);

  wire or_1_out;

  S_R_Flip_Flop s_r_ff_1 (.S(set), .clk(or_1_out), .R(reset), .Q(out_3));  // open: Qn, preset, reset, en
  or or_1 (or_1_out, set, reset);
endmodule

module tile_lock (
  input  set,
  input  reset,
  input  [7:0] in_3,
  input  enable,
  output out_5,
  output [7:0] out_6
);

  wire or_1_out, s_r_ff_1_q;
  wire [7:0] register_1_q;

  not not_1 (out_5, s_r_ff_1_q);
  S_R_Flip_Flop s_r_ff_1 (.S(set), .clk(or_1_out), .R(reset), .Q(s_r_ff_1_q), .en(enable));  // open: Qn, preset, reset
  or or_1 (or_1_out, set, reset);
  Register register_1 (.D(in_3), .Q(register_1_q), .clk(s_r_ff_1_q));  // open: en, clr
  Multiplexer #(.width(8), .enable("false")) multiplexer_1 (
    .in0(in_3), .in1(register_1_q), .out(out_6), .sel(s_r_ff_1_q));
endmodule

module manage_cubes_mirror (
  input  [2:0] in_1,
  input  [2:0] in_2,
  input  [2:0] in_3,
  input  [2:0] in_4,
  input  [2:0] in_5,
  input  enable,
  output [7:0] out_7,
  output [7:0] out_8,
  output [7:0] out_9,
  output [7:0] out_10,
  output [7:0] out_11,
  output [7:0] out_12,
  output [7:0] out_13,
  output [7:0] out_14,
  output [7:0] out_15,
  output [7:0] out_16,
  output [7:0] out_17
);

  manage_cubes manage_cubes_1 (
    .in_1(in_1), .in_2(in_2), .in_3(in_3), .in_4(in_4), .in_5(in_5), .out_7(out_7), .out_8(out_8),
    .out_9(out_9), .out_10(out_10), .out_11(out_11), .out_12(out_12), .out_13(out_13), .out_14(out_14),
    .out_15(out_15), .out_16(out_16), .out_17(out_17), .enable(enable));
endmodule

module tor (
  input  in_1,
  input  in_2,
  output out_3
);

  or or_1 (out_3, in_1, in_2);
endmodule

module tand_l (
  input  in_1,
  input  in_2,
  output out_3
);

  and and_1 (out_3, in_1, in_2);
endmodule

module tt (
  input  in_1,
  output out_2
);

  T_Flip_Flop t_ff_1 (.clk(in_1), .T(in_1), .Q(out_2));  // open: Qn, preset, reset, en
endmodule

module tor_l (
  input  in_1,
  input  in_2,
  output out_3
);

  or or_1 (out_3, in_1, in_2);
endmodule

module holder (
  input  hold,
  input  \release ,
  output out_3,
  output out_4
);

  niceSR nicesr_1 (.set(hold), .reset(\release ), .out_3(out_4));
  tand tand_1 (.in_1(out_4), .in_2(\release ), .out_3(out_3));
endmodule

module lollolol (
  input  in_1,
  input  in_2,
  input  in_3,
  input  in_4,
  input  in_5,
  input  in_6,
  input  in_7,
  input  in_8,
  input  in_9,
  input  in_10
);

  wire and_1_out, and_2_out, buffer_1_out, buffer_2_out, buffer_3_out, buffer_4_out, button_1_out,
       button_2_out, button_3_out, button_4_out, button_5_out, button_6_out, button_7_out, button_8_out,
       button_9_out, button_10_out, button_11_out, button_12_out, button_13_out, button_14_out,
       button_15_out, button_16_out, button_17_out, button_18_out, button_19_out, button_20_out,
       button_21_out, button_22_out, button_23_out, button_24_out, button_25_out, button_26_out,
       counter_1_carry, counter_2_carry, counter_3_carry, holder_1_out_3, holder_1_out_4, holder_2_out_3,
       holder_2_out_4, lol, nicesr_1_out_3, nicesr_2_out_3, not_1_out, not_2_out, not_3_out, not_4_out,
       not_5_out, not_6_out, not_7_out, not_8_out, not_9_out, not_10_out, not_11_out, not_12_out, not_13_out,
       not_14_out, not_15_out, not_16_out, or_2_out, or_3_out, random_1_out, start1, start2, start_out,
       t_ff_1_q, tand_1_out_3, tand_4_out_3, tand_l_1_out_3, tand_l_2_out_3, tand_l_3_out_3, tand_l_4_out_3,
       tand_l_5_out_3, tand_l_6_out_3, tand_l_7_out_3, tand_l_8_out_3, tand_l_9_out_3, tand_l_10_out_3,
       tand_l_11_out_3, tand_l_12_out_3, tand_l_13_out_3, tand_l_14_out_3, tand_l_15_out_3, tand_l_16_out_3,
       tand_l_17_out_3, tand_l_18_out_3, tand_l_19_out_3, tand_l_20_out_3, tand_l_21_out_3, tand_l_22_out_3,
       tand_l_23_out_3, tand_l_24_out_3, tand_l_25_out_3, tand_l_26_out_3, tand_l_27_out_3, tand_l_28_out_3,
       tand_l_29_out_3, tand_l_30_out_3, tand_l_31_out_3, tand_l_32_out_3, tand_l_33_out_3, tand_l_34_out_3,
       tand_l_35_out_3, tand_l_36_out_3, tand_l_37_out_3, tand_l_38_out_3, tand_l_39_out_3, tand_l_40_out_3,
       tand_l_41_out_3, tand_l_42_out_3, tand_l_43_out_3, tand_l_44_out_3, tile_lock_1_out_5,
       tile_lock_2_out_5, tile_lock_3_out_5, tile_lock_4_out_5, tile_lock_5_out_5, tile_lock_6_out_5,
       tile_lock_7_out_5, tile_lock_8_out_5, tile_lock_9_out_5, tile_lock_10_out_5, tile_lock_11_out_5,
       tile_lock_12_out_5, tile_lock_13_out_5, tile_lock_14_out_5, tile_lock_15_out_5, tile_lock_16_out_5,
       tile_lock_17_out_5, tile_lock_18_out_5, tile_lock_19_out_5, tile_lock_20_out_5, tile_lock_21_out_5,
       tile_lock_22_out_5, tor_1_out_3, tor_2_out_3, tor_3_out_3, tor_4_out_3, tor_5_out_3, tor_6_out_3,
       tor_7_out_3, tor_8_out_3, tor_9_out_3, tor_10_out_3, tor_l_1_out_3, tor_l_2_out_3, tt_1_out_2,
       tt_2_out_2;
  wire [2:0] _11, _12, _13, _14, _15, _21, _22, _23, _24, _25;
  wire [7:0] manage_cubes_mirror_1_out_7, manage_cubes_mirror_1_out_8, manage_cubes_mirror_1_out_9,
       manage_cubes_mirror_1_out_10, manage_cubes_mirror_1_out_11, manage_cubes_mirror_1_out_12,
       manage_cubes_mirror_1_out_13, manage_cubes_mirror_1_out_14, manage_cubes_mirror_1_out_15,
       manage_cubes_mirror_1_out_16, manage_cubes_mirror_1_out_17, manage_cubes_mirror_2_out_7,
       manage_cubes_mirror_2_out_8, manage_cubes_mirror_2_out_9, manage_cubes_mirror_2_out_10,
       manage_cubes_mirror_2_out_11, manage_cubes_mirror_2_out_12, manage_cubes_mirror_2_out_13,
       manage_cubes_mirror_2_out_14, manage_cubes_mirror_2_out_15, manage_cubes_mirror_2_out_16,
       manage_cubes_mirror_2_out_17, tile_lock_1_out_6, tile_lock_2_out_6, tile_lock_3_out_6,
       tile_lock_4_out_6, tile_lock_5_out_6, tile_lock_6_out_6, tile_lock_7_out_6, tile_lock_8_out_6,
       tile_lock_9_out_6, tile_lock_10_out_6, tile_lock_11_out_6, tile_lock_12_out_6, tile_lock_13_out_6,
       tile_lock_14_out_6, tile_lock_15_out_6, tile_lock_16_out_6, tile_lock_17_out_6, tile_lock_18_out_6,
       tile_lock_19_out_6, tile_lock_20_out_6, tile_lock_21_out_6, tile_lock_22_out_6;

  Button start (.out(start_out));
  or or_1 (lol, tand_l_1_out_3, tand_l_2_out_3, tand_l_3_out_3, tand_l_4_out_3, tand_l_5_out_3, tand_l_6_out_3, tand_l_7_out_3, tand_l_8_out_3, tand_l_9_out_3, tand_l_10_out_3, tand_l_11_out_3);
  tor tor_1 (.in_1(lol), .in_2(start1), .out_3(tor_1_out_3));
  Counter #(.width(1), .max('h1)) counter_1 (
    .carry(counter_1_carry), .clk(start_out), .clr(counter_1_carry));  // open: load, D, count, Q
  Random #(.width(1)) random_1 (.clk(start_out), .next(start_out), .out(random_1_out));  // open: clr
  tand_l tand_l_1 (.out_3(tand_l_1_out_3), .in_1(tand_l_12_out_3), .in_2(tor_2_out_3));
  tand_l tand_l_2 (.out_3(tand_l_2_out_3), .in_1(tand_l_13_out_3), .in_2(tor_2_out_3));
  tand_l tand_l_3 (.out_3(tand_l_3_out_3), .in_1(tand_l_14_out_3), .in_2(tor_2_out_3));
  tand_l tand_l_4 (.out_3(tand_l_4_out_3), .in_1(tand_l_15_out_3), .in_2(tor_2_out_3));
  tand_l tand_l_5 (.out_3(tand_l_5_out_3), .in_1(tand_l_16_out_3), .in_2(tor_2_out_3));
  tand_l tand_l_6 (.out_3(tand_l_6_out_3), .in_1(tand_l_17_out_3), .in_2(tor_2_out_3));
  tand_l tand_l_7 (.out_3(tand_l_7_out_3), .in_1(tand_l_18_out_3), .in_2(tor_2_out_3));
  tand_l tand_l_8 (.out_3(tand_l_8_out_3), .in_1(tand_l_19_out_3), .in_2(tor_2_out_3));
  tand_l tand_l_9 (.out_3(tand_l_9_out_3), .in_1(tand_l_20_out_3), .in_2(tor_2_out_3));
  tand_l tand_l_10 (.out_3(tand_l_10_out_3), .in_1(tand_l_21_out_3), .in_2(tor_2_out_3));
  tand_l tand_l_11 (.out_3(tand_l_11_out_3), .in_1(tand_l_22_out_3), .in_2(tor_2_out_3));
  Button button_1 (.out(button_1_out));
  tand tand_1 (.in_1(lol), .in_2(not_1_out), .out_3(tand_1_out_3));
  not not_1 (not_1_out, holder_1_out_4);
  holder holder_1 (.hold(counter_2_carry), .\release (tor_1_out_3), .out_3(holder_1_out_3), .out_4(holder_1_out_4));
  or or_2 (or_2_out, tor_1_out_3, holder_1_out_3, tor_7_out_3);
  tand tand_2 (.in_1(counter_1_carry), .in_2(random_1_out), .out_3(start1));
  tand tand_3 (.in_1(counter_1_carry), .in_2(not_2_out), .out_3(start2));
  not not_2 (not_2_out, random_1_out);
  tand_l tand_l_12 (.out_3(tand_l_12_out_3), .in_1(tile_lock_1_out_5), .in_2(button_2_out));
  tile_lock tile_lock_1 (
    .set(button_2_out), .reset(buffer_1_out), .enable(tor_2_out_3), .out_6(tile_lock_1_out_6),
    .in_3(manage_cubes_mirror_1_out_7), .out_5(tile_lock_1_out_5));
  // Probe on tile_lock_1_out_6
  Button button_2 (.out(button_2_out));
  // Probe on tile_lock_2_out_6
  tand_l tand_l_13 (.out_3(tand_l_13_out_3), .in_1(tile_lock_2_out_5), .in_2(button_3_out));
  tile_lock tile_lock_2 (
    .set(button_3_out), .reset(buffer_1_out), .enable(tor_2_out_3), .out_6(tile_lock_2_out_6),
    .in_3(manage_cubes_mirror_1_out_8), .out_5(tile_lock_2_out_5));
  Button button_3 (.out(button_3_out));
  tand_l tand_l_14 (.out_3(tand_l_14_out_3), .in_1(tile_lock_3_out_5), .in_2(button_4_out));
  // Probe on tile_lock_3_out_6
  tile_lock tile_lock_3 (
    .set(button_4_out), .reset(buffer_1_out), .enable(tor_2_out_3), .out_6(tile_lock_3_out_6),
    .in_3(manage_cubes_mirror_1_out_9), .out_5(tile_lock_3_out_5));
  Button button_4 (.out(button_4_out));
  tile_lock tile_lock_4 (
    .set(button_5_out), .reset(buffer_1_out), .enable(tor_2_out_3), .out_6(tile_lock_4_out_6),
    .in_3(manage_cubes_mirror_1_out_10), .out_5(tile_lock_4_out_5));
  // Probe on tile_lock_4_out_6
  tand_l tand_l_15 (.out_3(tand_l_15_out_3), .in_1(tile_lock_4_out_5), .in_2(button_5_out));
  Button button_5 (.out(button_5_out));
  tile_lock tile_lock_5 (
    .set(button_6_out), .reset(buffer_1_out), .enable(tor_2_out_3), .out_6(tile_lock_5_out_6),
    .in_3(manage_cubes_mirror_1_out_11), .out_5(tile_lock_5_out_5));
  // Probe on tile_lock_5_out_6
  tand_l tand_l_16 (.out_3(tand_l_16_out_3), .in_1(tile_lock_5_out_5), .in_2(button_6_out));
  Button button_6 (.out(button_6_out));
  // Probe on tile_lock_6_out_6
  tile_lock tile_lock_6 (
    .set(button_7_out), .reset(buffer_1_out), .enable(tor_2_out_3), .out_6(tile_lock_6_out_6),
    .in_3(manage_cubes_mirror_1_out_12), .out_5(tile_lock_6_out_5));
  tand_l tand_l_17 (.out_3(tand_l_17_out_3), .in_1(tile_lock_6_out_5), .in_2(button_7_out));
  Button button_7 (.out(button_7_out));
  tile_lock tile_lock_7 (
    .set(button_8_out), .reset(buffer_1_out), .enable(tor_2_out_3), .out_6(tile_lock_7_out_6),
    .in_3(manage_cubes_mirror_1_out_13), .out_5(tile_lock_7_out_5));
  // Probe on tile_lock_7_out_6
  tand_l tand_l_18 (.out_3(tand_l_18_out_3), .in_1(tile_lock_7_out_5), .in_2(button_8_out));
  Button button_8 (.out(button_8_out));
  tand_l tand_l_19 (.out_3(tand_l_19_out_3), .in_1(tile_lock_8_out_5), .in_2(button_9_out));
  // Probe on tile_lock_8_out_6
  tile_lock tile_lock_8 (
    .set(button_9_out), .reset(buffer_1_out), .enable(tor_2_out_3), .out_6(tile_lock_8_out_6),
    .in_3(manage_cubes_mirror_1_out_14), .out_5(tile_lock_8_out_5));
  Button button_9 (.out(button_9_out));
  tile_lock tile_lock_9 (
    .set(button_10_out), .reset(buffer_1_out), .enable(tor_2_out_3), .out_6(tile_lock_9_out_6),
    .in_3(manage_cubes_mirror_1_out_15), .out_5(tile_lock_9_out_5));
  // Probe on tile_lock_9_out_6
  tand_l tand_l_20 (.out_3(tand_l_20_out_3), .in_1(tile_lock_9_out_5), .in_2(button_10_out));
  Button button_10 (.out(button_10_out));
  tile_lock tile_lock_10 (
    .set(button_11_out), .reset(buffer_1_out), .enable(tor_2_out_3), .out_6(tile_lock_10_out_6),
    .in_3(manage_cubes_mirror_1_out_16), .out_5(tile_lock_10_out_5));
  tand_l tand_l_21 (.out_3(tand_l_21_out_3), .in_1(tile_lock_10_out_5), .in_2(button_11_out));
  // Probe on tile_lock_10_out_6
  Button button_11 (.out(button_11_out));
  // Probe on tile_lock_11_out_6
  tand_l tand_l_22 (.out_3(tand_l_22_out_3), .in_1(tile_lock_11_out_5), .in_2(button_12_out));
  tile_lock tile_lock_11 (
    .set(button_12_out), .reset(buffer_1_out), .enable(tor_2_out_3), .out_6(tile_lock_11_out_6),
    .in_3(manage_cubes_mirror_1_out_17), .out_5(tile_lock_11_out_5));
  Button button_12 (.out(button_12_out));
  buf buffer_1 (buffer_1_out, buffer_2_out);
  tor tor_2 (.in_1(button_1_out), .in_2(t_ff_1_q), .out_3(tor_2_out_3));
  buf buffer_2 (buffer_2_out, button_1_out);
  tt tt_1 (.in_1(tor_3_out_3), .out_2(tt_1_out_2));
  tor tor_3 (.in_1(tor_l_1_out_3), .in_2(tand_1_out_3), .out_3(tor_3_out_3));
  Button button_13 (.out(button_13_out));
  not not_3 (not_3_out, in_1);
  not not_4 (not_4_out, in_3);
  not not_5 (not_5_out, in_5);
  not not_6 (not_6_out, in_7);
  not not_7 (not_7_out, in_9);
  niceSR nicesr_1 (.set(and_1_out), .reset(not_8_out), .out_3(nicesr_1_out_3));
  not not_8 (not_8_out, t_ff_1_q);
  T_Flip_Flop t_ff_1 (.clk(or_2_out), .T(or_2_out), .Q(t_ff_1_q));  // open: Qn, preset, reset, en
  manage_cubes_mirror manage_cubes_mirror_1 (
    .in_1(_11), .in_2(_12), .in_3(_13), .in_4(_14), .in_5(_15), .out_7(manage_cubes_mirror_1_out_7),
    .out_8(manage_cubes_mirror_1_out_8), .out_9(manage_cubes_mirror_1_out_9),
    .out_10(manage_cubes_mirror_1_out_10), .out_11(manage_cubes_mirror_1_out_11),
    .out_12(manage_cubes_mirror_1_out_12), .out_13(manage_cubes_mirror_1_out_13),
    .out_14(manage_cubes_mirror_1_out_14), .out_15(manage_cubes_mirror_1_out_15),
    .out_16(manage_cubes_mirror_1_out_16), .out_17(manage_cubes_mirror_1_out_17), .enable(t_ff_1_q));
  or or_3 (or_3_out, tand_l_23_out_3, tand_l_25_out_3, tand_l_28_out_3, tand_l_30_out_3, tand_l_32_out_3, tand_l_33_out_3, tand_l_36_out_3, tand_l_37_out_3, tand_l_39_out_3, tand_l_41_out_3, tand_l_44_out_3);
  tor tor_4 (.in_1(or_3_out), .in_2(start1), .out_3(tor_4_out_3));
  tor_l tor_l_1 (.out_3(tor_l_1_out_3), .in_1(tor_4_out_3), .in_2(counter_2_carry));
  Counter #(.width(2), .max('h3)) counter_2 (
    .carry(counter_2_carry), .clk(and_1_out), .clr(tor_5_out_3));  // open: load, D, count, Q
  and and_1 (and_1_out, tt_1_out_2, button_13_out);
  tor tor_5 (.in_1(tor_1_out_3), .in_2(counter_2_carry), .out_3(tor_5_out_3));
  // Probe on _11
  player_panel player_panel_1 (
    .in_2(not_3_out), .out_9(_11), .out_10(_12), .out_11(_13), .out_12(_14), .out_13(_15), .Roll(and_1_out),
    .in_3(not_4_out), .in_4(not_5_out), .in_5(not_6_out), .in_6(not_7_out), .Enable(t_ff_1_q),
    .Enable_cubes(nicesr_1_out_3));
  // Probe on _12
  // Probe on _13
  // Probe on _14
  // Probe on _15
  tand_l tand_l_23 (.out_3(tand_l_23_out_3), .in_1(tand_l_24_out_3), .in_2(tor_6_out_3));
  tand_l tand_l_24 (.out_3(tand_l_24_out_3), .in_1(tile_lock_12_out_5), .in_2(button_15_out));
  tand_l tand_l_25 (.out_3(tand_l_25_out_3), .in_1(tand_l_26_out_3), .in_2(tor_6_out_3));
  tand_l tand_l_26 (.out_3(tand_l_26_out_3), .in_1(tile_lock_13_out_5), .in_2(button_16_out));
  tand_l tand_l_27 (.out_3(tand_l_27_out_3), .in_1(tile_lock_14_out_5), .in_2(button_17_out));
  tand_l tand_l_28 (.out_3(tand_l_28_out_3), .in_1(tand_l_27_out_3), .in_2(tor_6_out_3));
  tand_l tand_l_29 (.out_3(tand_l_29_out_3), .in_1(tile_lock_15_out_5), .in_2(button_18_out));
  tand_l tand_l_30 (.out_3(tand_l_30_out_3), .in_1(tand_l_29_out_3), .in_2(tor_6_out_3));
  tand_l tand_l_31 (.out_3(tand_l_31_out_3), .in_1(tile_lock_16_out_5), .in_2(button_19_out));
  tand_l tand_l_32 (.out_3(tand_l_32_out_3), .in_1(tand_l_31_out_3), .in_2(tor_6_out_3));
  tand_l tand_l_33 (.out_3(tand_l_33_out_3), .in_1(tand_l_34_out_3), .in_2(tor_6_out_3));
  tand_l tand_l_34 (.out_3(tand_l_34_out_3), .in_1(tile_lock_17_out_5), .in_2(button_20_out));
  tand_l tand_l_35 (.out_3(tand_l_35_out_3), .in_1(tile_lock_18_out_5), .in_2(button_21_out));
  tand_l tand_l_36 (.out_3(tand_l_36_out_3), .in_1(tand_l_35_out_3), .in_2(tor_6_out_3));
  tand_l tand_l_37 (.out_3(tand_l_37_out_3), .in_1(tand_l_38_out_3), .in_2(tor_6_out_3));
  tand_l tand_l_38 (.out_3(tand_l_38_out_3), .in_1(tile_lock_19_out_5), .in_2(button_22_out));
  tand_l tand_l_39 (.out_3(tand_l_39_out_3), .in_1(tand_l_40_out_3), .in_2(tor_6_out_3));
  tand_l tand_l_40 (.out_3(tand_l_40_out_3), .in_1(tile_lock_20_out_5), .in_2(button_23_out));
  tand_l tand_l_41 (.out_3(tand_l_41_out_3), .in_1(tand_l_42_out_3), .in_2(tor_6_out_3));
  tand_l tand_l_42 (.out_3(tand_l_42_out_3), .in_1(tile_lock_21_out_5), .in_2(button_24_out));
  tand_l tand_l_43 (.out_3(tand_l_43_out_3), .in_1(tile_lock_22_out_5), .in_2(button_25_out));
  tand_l tand_l_44 (.out_3(tand_l_44_out_3), .in_1(tand_l_43_out_3), .in_2(tor_6_out_3));
  tor tor_6 (.in_1(button_14_out), .in_2(not_10_out), .out_3(tor_6_out_3));
  Button button_14 (.out(button_14_out));
  tand tand_4 (.in_1(or_3_out), .in_2(not_9_out), .out_3(tand_4_out_3));
  not not_9 (not_9_out, holder_2_out_4);
  holder holder_2 (.hold(counter_3_carry), .\release (or_3_out), .out_3(holder_2_out_3), .out_4(holder_2_out_4));
  tor tor_7 (.in_1(holder_2_out_3), .in_2(or_3_out), .out_3(tor_7_out_3));
  not not_10 (not_10_out, t_ff_1_q);
  // Probe on tile_lock_12_out_6
  tile_lock tile_lock_12 (
    .set(button_15_out), .reset(buffer_3_out), .enable(tor_6_out_3), .out_6(tile_lock_12_out_6),
    .in_3(manage_cubes_mirror_2_out_7), .out_5(tile_lock_12_out_5));
  manage_cubes_mirror manage_cubes_mirror_2 (
    .in_1(_21), .in_2(_22), .in_3(_23), .in_4(_24), .in_5(_25), .out_7(manage_cubes_mirror_2_out_7),
    .out_8(manage_cubes_mirror_2_out_8), .out_9(manage_cubes_mirror_2_out_9),
    .out_10(manage_cubes_mirror_2_out_10), .out_11(manage_cubes_mirror_2_out_11),
    .out_12(manage_cubes_mirror_2_out_12), .out_13(manage_cubes_mirror_2_out_13),
    .out_14(manage_cubes_mirror_2_out_14), .out_15(manage_cubes_mirror_2_out_15),
    .out_16(manage_cubes_mirror_2_out_16), .out_17(manage_cubes_mirror_2_out_17), .enable(not_10_out));
  Button button_15 (.out(button_15_out));
  tile_lock tile_lock_13 (
    .set(button_16_out), .reset(buffer_3_out), .enable(tor_6_out_3), .out_6(tile_lock_13_out_6),
    .in_3(manage_cubes_mirror_2_out_8), .out_5(tile_lock_13_out_5));
  // Probe on tile_lock_13_out_6
  Button button_16 (.out(button_16_out));
  tile_lock tile_lock_14 (
    .set(button_17_out), .reset(buffer_3_out), .enable(tor_6_out_3), .out_6(tile_lock_14_out_6),
    .in_3(manage_cubes_mirror_2_out_9), .out_5(tile_lock_14_out_5));
  // Probe on tile_lock_14_out_6
  Button button_17 (.out(button_17_out));
  tile_lock tile_lock_15 (
    .set(button_18_out), .reset(buffer_3_out), .enable(tor_6_out_3), .out_6(tile_lock_15_out_6),
    .in_3(manage_cubes_mirror_2_out_10), .out_5(tile_lock_15_out_5));
  // Probe on tile_lock_15_out_6
  Button button_18 (.out(button_18_out));
  tile_lock tile_lock_16 (
    .set(button_19_out), .reset(buffer_3_out), .enable(tor_6_out_3), .out_6(tile_lock_16_out_6),
    .in_3(manage_cubes_mirror_2_out_11), .out_5(tile_lock_16_out_5));
  // Probe on tile_lock_16_out_6
  Button button_19 (.out(button_19_out));
  tile_lock tile_lock_17 (
    .set(button_20_out), .reset(buffer_3_out), .enable(tor_6_out_3), .out_6(tile_lock_17_out_6),
    .in_3(manage_cubes_mirror_2_out_12), .out_5(tile_lock_17_out_5));
  // Probe on tile_lock_17_out_6
  Button button_20 (.out(button_20_out));
  tile_lock tile_lock_18 (
    .set(button_21_out), .reset(buffer_3_out), .enable(tor_6_out_3), .out_6(tile_lock_18_out_6),
    .in_3(manage_cubes_mirror_2_out_13), .out_5(tile_lock_18_out_5));
  // Probe on tile_lock_18_out_6
  Button button_21 (.out(button_21_out));
  tile_lock tile_lock_19 (
    .set(button_22_out), .reset(buffer_3_out), .enable(tor_6_out_3), .out_6(tile_lock_19_out_6),
    .in_3(manage_cubes_mirror_2_out_14), .out_5(tile_lock_19_out_5));
  // Probe on tile_lock_19_out_6
  Button button_22 (.out(button_22_out));
  tile_lock tile_lock_20 (
    .set(button_23_out), .reset(buffer_3_out), .enable(tor_6_out_3), .out_6(tile_lock_20_out_6),
    .in_3(manage_cubes_mirror_2_out_15), .out_5(tile_lock_20_out_5));
  // Probe on tile_lock_20_out_6
  Button button_23 (.out(button_23_out));
  // Probe on tile_lock_21_out_6
  tile_lock tile_lock_21 (
    .set(button_24_out), .reset(buffer_3_out), .enable(tor_6_out_3), .out_6(tile_lock_21_out_6),
    .in_3(manage_cubes_mirror_2_out_16), .out_5(tile_lock_21_out_5));
  Button button_24 (.out(button_24_out));
  // Probe on tile_lock_22_out_6
  tile_lock tile_lock_22 (
    .set(button_25_out), .reset(buffer_3_out), .enable(tor_6_out_3), .out_6(tile_lock_22_out_6),
    .in_3(manage_cubes_mirror_2_out_17), .out_5(tile_lock_22_out_5));
  Button button_25 (.out(button_25_out));
  buf buffer_3 (buffer_3_out, buffer_4_out);
  buf buffer_4 (buffer_4_out, button_14_out);
  tor tor_8 (.in_1(tor_l_2_out_3), .in_2(tand_4_out_3), .out_3(tor_8_out_3));
  tt tt_2 (.in_1(tor_8_out_3), .out_2(tt_2_out_2));
  and and_2 (and_2_out, tt_2_out_2, button_26_out);
  Button button_26 (.out(button_26_out));
  player_panel2 player_panel2_1 (
    .in_2(not_11_out), .in_3(not_12_out), .in_4(not_13_out), .in_5(not_14_out), .in_6(not_15_out),
    .out_9(_21), .out_10(_22), .out_11(_23), .out_12(_24), .out_13(_25), .Roll(and_2_out),
    .Enable(not_10_out), .Enable_cubes(nicesr_2_out_3));
  not not_11 (not_11_out, in_2);
  not not_12 (not_12_out, in_4);
  not not_13 (not_13_out, in_6);
  not not_14 (not_14_out, in_8);
  not not_15 (not_15_out, in_10);
  niceSR nicesr_2 (.set(and_2_out), .reset(not_16_out), .out_3(nicesr_2_out_3));
  not not_16 (not_16_out, not_10_out);
  tor tor_9 (.in_1(lol), .in_2(start2), .out_3(tor_9_out_3));
  tor_l tor_l_2 (.out_3(tor_l_2_out_3), .in_1(tor_9_out_3), .in_2(counter_3_carry));
  Counter #(.width(2), .max('h3)) counter_3 (
    .carry(counter_3_carry), .clk(and_2_out), .clr(tor_10_out_3));  // open: load, D, count, Q
  tor tor_10 (.in_1(or_3_out), .in_2(counter_3_carry), .out_3(tor_10_out_3));
  // Probe on _21
  // Probe on _22
  // Probe on _23
  // Probe on _24
  // Probe on _25
endmodule

module D6_better (
  input  roll,
  input  enable,
  input  [7:0] in_3,
  output [2:0] out_4
);

  wire comparator_1_lt, comparator_2_lt, comparator_3_lt, comparator_4_lt, comparator_5_lt,
       pull_resistor_1_node, pull_resistor_5_node, transistor_1_out, transistor_2_out, transistor_3_out,
       transistor_4_out, transistor_5_out, transistor_6_out, transistor_7_out, transistor_8_out,
       transistor_9_out, transistor_10_out, transistor_12_out, transistor_13_out, transistor_14_out;
  wire [2:0] adder_1_out, adder_2_out, adder_3_out, adder_4_out, multiplexer_1_out, multiplexer_2_out,
       multiplexer_3_out, multiplexer_4_out, multiplexer_5_out, multiplexer_6_out;
  wire [4:0] bit_extender_1_out;
  wire [31:0] random_1_out, shifter_1_out;

  Bit_Extender #(.out_width(5)) bit_extender_1 (.in(in_3), .out(bit_extender_1_out));
  Random #(.width(32)) random_1 (.clk(roll), .next(enable), .out(random_1_out), .clr(1'b0));
  Shifter #(.width(32), .shift("rl")) shifter_1 (.in(random_1_out), .\dist (bit_extender_1_out), .out(shifter_1_out));
  Comparator #(.width(32), .mode("unsigned")) comparator_1 (
    .a(shifter_1_out), .b(32'h2aaaaaaa), .lt(comparator_1_lt));  // open: gt, eq
  Comparator #(.width(32), .mode("unsigned")) comparator_2 (
    .a(shifter_1_out), .b(32'h55555555), .lt(comparator_2_lt));  // open: gt, eq
  Comparator #(.width(32), .mode("unsigned")) comparator_3 (
    .a(shifter_1_out), .b(32'h80000000), .lt(comparator_3_lt));  // open: gt, eq
  Comparator #(.width(32), .mode("unsigned")) comparator_4 (
    .a(shifter_1_out), .b(32'haaaaaaaa), .lt(comparator_4_lt));  // open: gt, eq
  Comparator #(.width(32), .mode("unsigned")) comparator_5 (
    .a(shifter_1_out), .b(32'hd5555555), .lt(comparator_5_lt));  // open: gt, eq
  Transistor transistor_1 (.in(comparator_5_lt), .out(transistor_1_out), .gate(comparator_4_lt));
  Transistor transistor_2 (.in(1'b1), .out(transistor_2_out), .gate(comparator_5_lt));
  Transistor transistor_3 (.in(transistor_2_out), .out(transistor_3_out), .gate(comparator_4_lt));
  Transistor transistor_4 (.in(comparator_3_lt), .out(transistor_4_out), .gate(comparator_2_lt));
  Transistor transistor_5 (.in(transistor_6_out), .out(transistor_5_out), .gate(comparator_2_lt));
  Transistor transistor_6 (.in(comparator_4_lt), .out(transistor_6_out), .gate(comparator_3_lt));
  Transistor transistor_7 (.in(transistor_8_out), .out(transistor_7_out), .gate(comparator_2_lt));
  Transistor transistor_8 (.in(transistor_1_out), .out(transistor_8_out), .gate(comparator_3_lt));
  Transistor transistor_9 (.in(transistor_10_out), .out(transistor_9_out), .gate(comparator_2_lt));
  Transistor transistor_10 (.in(transistor_3_out), .out(transistor_10_out), .gate(comparator_3_lt));
  Pull_Resistor pull_resistor_1 (.node(pull_resistor_1_node));
  Transistor transistor_11 (.in(comparator_2_lt), .out(pull_resistor_1_node), .gate(comparator_1_lt));
  Transistor transistor_12 (.in(transistor_4_out), .out(transistor_12_out), .gate(comparator_1_lt));
  Pull_Resistor pull_resistor_2 (.node(transistor_12_out));
  Transistor transistor_13 (.in(transistor_5_out), .out(transistor_13_out), .gate(comparator_1_lt));
  Pull_Resistor pull_resistor_3 (.node(transistor_13_out));
  Transistor transistor_14 (.in(transistor_7_out), .out(transistor_14_out), .gate(comparator_1_lt));
  Pull_Resistor pull_resistor_4 (.node(transistor_14_out));
  Pull_Resistor pull_resistor_5 (.node(pull_resistor_5_node));
  Transistor transistor_15 (.in(transistor_9_out), .out(pull_resistor_5_node), .gate(comparator_1_lt));
  Multiplexer #(.width(3), .enable("false")) multiplexer_1 (
    .in0(3'b000), .in1(3'b001), .out(multiplexer_1_out), .sel(comparator_1_lt));
  Adder #(.width(3)) adder_1 (
    .a(multiplexer_1_out), .b(multiplexer_2_out), .out(adder_1_out), .cin(1'b0));  // open: cout
  Multiplexer #(.width(3), .enable("false")) multiplexer_2 (
    .in0(3'b000), .in1(3'b010), .out(multiplexer_2_out), .sel(pull_resistor_1_node));
  Multiplexer #(.width(3), .enable("false")) multiplexer_3 (
    .in0(3'b000), .in1(3'b011), .out(multiplexer_3_out), .sel(transistor_12_out));
  Adder #(.width(3)) adder_2 (
    .a(multiplexer_3_out), .b(multiplexer_4_out), .out(adder_2_out), .cin(1'b0));  // open: cout
  Multiplexer #(.width(3), .enable("false")) multiplexer_4 (
    .in0(3'b000), .in1(3'b100), .out(multiplexer_4_out), .sel(transistor_13_out));
  Multiplexer #(.width(3), .enable("false")) multiplexer_5 (
    .in0(3'b000), .in1(3'b101), .out(multiplexer_5_out), .sel(transistor_14_out));
  Adder #(.width(3)) adder_3 (
    .a(multiplexer_5_out), .b(multiplexer_6_out), .out(adder_3_out), .cin(1'b0));  // open: cout
  Multiplexer #(.width(3), .enable("false")) multiplexer_6 (
    .in0(3'b000), .in1(3'b110), .out(multiplexer_6_out), .sel(pull_resistor_5_node));
  Adder #(.width(3)) adder_4 (.a(adder_1_out), .b(adder_2_out), .out(adder_4_out), .cin(1'b0));  // open: cout
  Adder #(.width(3)) adder_5 (.a(adder_4_out), .b(adder_3_out), .out(out_4), .cin(1'b0));  // open: cout
endmodule

module player_panel2 (
  input  Roll,
  input  in_2,
  input  in_3,
  input  in_4,
  input  in_5,
  input  in_6,
  input  Enable,
  input  Enable_cubes,
  output [2:0] out_9,
  output [2:0] out_10,
  output [2:0] out_11,
  output [2:0] out_12,
  output [2:0] out_13
);

  wire and_1_out, button_1_out, not_1_out;
  wire [2:0] d6_1_out_4, d6_2_out_4, d6_3_out_4, d6_4_out_4, d6_5_out_4;
  wire [7:0] random_1_out, random_2_out, random_3_out, random_4_out, random_5_out;

  Button button_1 (.out(button_1_out));
  Random #(.seed(90)) random_1 (.clk(and_1_out), .next(in_2), .out(random_1_out), .clr(button_1_out));
  Random #(.seed(690)) random_2 (.clk(and_1_out), .next(in_3), .out(random_2_out), .clr(button_1_out));
  Random #(.seed(4200)) random_3 (.clk(and_1_out), .next(in_4), .out(random_3_out), .clr(button_1_out));
  Random #(.seed(13370)) random_4 (.clk(and_1_out), .next(in_5), .out(random_4_out), .clr(button_1_out));
  Random #(.seed(9990)) random_5 (.clk(and_1_out), .next(in_6), .out(random_5_out), .clr(button_1_out));
  and and_1 (and_1_out, Enable, Roll);
  D6 d6_1 (.roll(and_1_out), .in_2(random_1_out), .enable(in_2), .out_4(d6_1_out_4));
  D6 d6_2 (.roll(and_1_out), .in_2(random_2_out), .enable(in_3), .out_4(d6_2_out_4));
  D6 d6_3 (.roll(and_1_out), .in_2(random_3_out), .enable(in_4), .out_4(d6_3_out_4));
  D6 d6_4 (.roll(and_1_out), .in_2(random_4_out), .enable(in_5), .out_4(d6_4_out_4));
  D6 d6_5 (.roll(and_1_out), .in_2(random_5_out), .enable(in_6), .out_4(d6_5_out_4));
  // Probe on d6_1_out_4
  Multiplexer #(.width(3), .enable("false")) multiplexer_1 (
    .in0(d6_1_out_4), .in1(3'b000), .out(out_9), .sel(not_1_out));
  // Probe on d6_2_out_4
  Multiplexer #(.width(3), .enable("false")) multiplexer_2 (
    .in0(d6_2_out_4), .in1(3'b000), .out(out_10), .sel(not_1_out));
  // Probe on d6_3_out_4
  Multiplexer #(.width(3), .enable("false")) multiplexer_3 (
    .in0(d6_3_out_4), .in1(3'b000), .out(out_11), .sel(not_1_out));
  // Probe on d6_4_out_4
  Multiplexer #(.width(3), .enable("false")) multiplexer_4 (
    .in0(d6_4_out_4), .in1(3'b000), .out(out_12), .sel(not_1_out));
  // Probe on d6_5_out_4
  Multiplexer #(.width(3), .enable("false")) multiplexer_5 (
    .in0(d6_5_out_4), .in1(3'b000), .out(out_13), .sel(not_1_out));
  not not_1 (not_1_out, Enable_cubes);
endmodule

module kok (
  input  in_1,
  input  in_2,
  input  in_3,
  input  in_4,
  input  in_5,
  input  in_6,
  input  in_7,
  input  in_8,
  input  in_9,
  input  in_10,
  input  in_11,
  input  reset,
  input  start,
  input  other_done,
  input  roll,
  input  in_16,
  input  in_17,
  input  in_18,
  input  in_19,
  input  in_20,
  input  enable,
  output out_22,
  output [7:0] out_23,
  output out_24,
  output [7:0] out_25,
  output out_26,
  output [7:0] out_27,
  output out_28,
  output [7:0] out_29,
  output out_30,
  output [7:0] out_31,
  output out_32,
  output [7:0] out_33,
  output out_34,
  output [7:0] out_35,
  output out_36,
  output [7:0] out_37,
  output out_38,
  output [7:0] out_39,
  output out_40,
  output [7:0] out_41,
  output out_42,
  output [7:0] out_43,
  output done,
  output roll_enabled,
  output [2:0] out_46,
  output out_47,
  output [2:0] out_48,
  output out_49,
  output [2:0] out_50,
  output out_51,
  output [2:0] out_52,
  output out_53,
  output [2:0] out_54,
  output out_55,
  output swap
);

  wire and_1_out, buffer_1_out, buffer_2_out, counter_1_carry, holder_1_out_3, holder_1_out_4,
       nicesr_1_out_3, not_1_out, not_2_out, not_3_out, not_4_out, not_5_out, not_6_out, not_7_out, or_2_out,
       or_3_out, tand_1_out_3, tand_2_out_3, tand_3_out_3, tand_4_out_3, tand_5_out_3, tand_6_out_3,
       tand_l_1_out_3, tand_l_2_out_3, tand_l_3_out_3, tand_l_4_out_3, tand_l_5_out_3, tand_l_6_out_3,
       tand_l_7_out_3, tand_l_8_out_3, tand_l_9_out_3, tand_l_10_out_3, tand_l_11_out_3, tand_l_12_out_3,
       tand_l_13_out_3, tand_l_14_out_3, tand_l_15_out_3, tand_l_16_out_3, tand_l_17_out_3, tand_l_18_out_3,
       tand_l_19_out_3, tand_l_20_out_3, tand_l_21_out_3, tand_l_22_out_3, tor_1_out_3, tor_2_out_3,
       tor_3_out_3, tor_4_out_3, tor_5_out_3, tor_6_out_3, tor_7_out_3, tor_8_out_3, tor_9_out_3,
       tor_l_1_out_3;
  wire [7:0] manage_cubes_mirror_1_out_7, manage_cubes_mirror_1_out_8, manage_cubes_mirror_1_out_9,
       manage_cubes_mirror_1_out_10, manage_cubes_mirror_1_out_11, manage_cubes_mirror_1_out_12,
       manage_cubes_mirror_1_out_13, manage_cubes_mirror_1_out_14, manage_cubes_mirror_1_out_15,
       manage_cubes_mirror_1_out_16, manage_cubes_mirror_1_out_17;

  or or_1 (done, tand_l_1_out_3, tand_l_2_out_3, tand_l_3_out_3, tand_l_4_out_3, tand_l_5_out_3, tand_l_6_out_3, tand_l_7_out_3, tand_l_8_out_3, tand_l_9_out_3, tand_l_10_out_3, tand_l_11_out_3);
  or or_2 (or_2_out, or_3_out, roll);
  or or_3 (or_3_out, in_1, in_4, in_2, in_5, in_3, in_6, in_9, in_7, in_10, in_8, in_11);
  tand_l tand_l_1 (.out_3(tand_l_1_out_3), .in_1(tand_l_12_out_3), .in_2(tor_6_out_3));
  tand_l tand_l_2 (.out_3(tand_l_2_out_3), .in_1(tand_l_13_out_3), .in_2(tor_6_out_3));
  tand_l tand_l_3 (.out_3(tand_l_3_out_3), .in_1(tand_l_14_out_3), .in_2(tor_6_out_3));
  tand_l tand_l_4 (.out_3(tand_l_4_out_3), .in_1(tand_l_15_out_3), .in_2(tor_6_out_3));
  tand_l tand_l_5 (.out_3(tand_l_5_out_3), .in_1(tand_l_16_out_3), .in_2(tor_6_out_3));
  tand_l tand_l_6 (.out_3(tand_l_6_out_3), .in_1(tand_l_17_out_3), .in_2(tor_6_out_3));
  tand_l tand_l_7 (.out_3(tand_l_7_out_3), .in_1(tand_l_18_out_3), .in_2(tor_6_out_3));
  tand_l tand_l_8 (.out_3(tand_l_8_out_3), .in_1(tand_l_19_out_3), .in_2(tor_6_out_3));
  tand_l tand_l_9 (.out_3(tand_l_9_out_3), .in_1(tand_l_20_out_3), .in_2(tor_6_out_3));
  tand_l tand_l_10 (.out_3(tand_l_10_out_3), .in_1(tand_l_21_out_3), .in_2(tor_6_out_3));
  tand_l tand_l_11 (.out_3(tand_l_11_out_3), .in_1(tand_l_22_out_3), .in_2(tor_6_out_3));
  tand tand_1 (.in_1(done), .in_2(not_1_out), .out_3(tand_1_out_3));
  not not_1 (not_1_out, holder_1_out_4);
  holder holder_1 (.hold(counter_1_carry), .\release (done), .out_3(holder_1_out_3), .out_4(holder_1_out_4));
  tor tor_1 (.in_1(in_16), .in_2(tand_2_out_3), .out_3(tor_1_out_3));
  tt tt_1 (.in_1(tor_1_out_3), .out_2(out_47));
  tand tand_2 (.in_1(or_2_out), .in_2(out_47), .out_3(tand_2_out_3));
  or or_4 (swap, done, holder_1_out_3);
  tt tt_2 (.in_1(tor_2_out_3), .out_2(out_49));
  tor tor_2 (.in_1(in_17), .in_2(tand_3_out_3), .out_3(tor_2_out_3));
  tand tand_3 (.in_1(or_2_out), .in_2(out_49), .out_3(tand_3_out_3));
  tt tt_3 (.in_1(tor_3_out_3), .out_2(out_51));
  tor tor_3 (.in_1(in_18), .in_2(tand_4_out_3), .out_3(tor_3_out_3));
  tand tand_4 (.in_1(or_2_out), .in_2(out_51), .out_3(tand_4_out_3));
  tor tor_4 (.in_1(in_19), .in_2(tand_5_out_3), .out_3(tor_4_out_3));
  tt tt_4 (.in_1(tor_4_out_3), .out_2(out_53));
  tand tand_5 (.in_1(or_2_out), .in_2(out_53), .out_3(tand_5_out_3));
  tor tor_5 (.in_1(in_20), .in_2(tand_6_out_3), .out_3(tor_5_out_3));
  tt tt_5 (.in_1(tor_5_out_3), .out_2(out_55));
  tand tand_6 (.in_1(or_2_out), .in_2(out_55), .out_3(tand_6_out_3));
  tand_l tand_l_12 (.out_3(tand_l_12_out_3), .in_1(out_22), .in_2(in_1));
  tile_lock tile_lock_1 (
    .set(in_1), .reset(buffer_1_out), .enable(tor_6_out_3), .out_6(out_23),
    .in_3(manage_cubes_mirror_1_out_7), .out_5(out_22));
  tile_lock tile_lock_2 (
    .set(in_2), .reset(buffer_1_out), .enable(tor_6_out_3), .out_6(out_25),
    .in_3(manage_cubes_mirror_1_out_8), .out_5(out_24));
  tand_l tand_l_13 (.out_3(tand_l_13_out_3), .in_1(out_24), .in_2(in_2));
  tile_lock tile_lock_3 (
    .set(in_3), .reset(buffer_1_out), .enable(tor_6_out_3), .out_6(out_27),
    .in_3(manage_cubes_mirror_1_out_9), .out_5(out_26));
  tand_l tand_l_14 (.out_3(tand_l_14_out_3), .in_1(out_26), .in_2(in_3));
  tile_lock tile_lock_4 (
    .set(in_4), .reset(buffer_1_out), .enable(tor_6_out_3), .out_6(out_29),
    .in_3(manage_cubes_mirror_1_out_10), .out_5(out_28));
  tand_l tand_l_15 (.out_3(tand_l_15_out_3), .in_1(out_28), .in_2(in_4));
  tand_l tand_l_16 (.out_3(tand_l_16_out_3), .in_1(out_30), .in_2(in_5));
  tile_lock tile_lock_5 (
    .set(in_5), .reset(buffer_1_out), .enable(tor_6_out_3), .out_6(out_31),
    .in_3(manage_cubes_mirror_1_out_11), .out_5(out_30));
  tand_l tand_l_17 (.out_3(tand_l_17_out_3), .in_1(out_32), .in_2(in_6));
  tile_lock tile_lock_6 (
    .set(in_6), .reset(buffer_1_out), .enable(tor_6_out_3), .out_6(out_33),
    .in_3(manage_cubes_mirror_1_out_12), .out_5(out_32));
  tile_lock tile_lock_7 (
    .set(in_7), .reset(buffer_1_out), .enable(tor_6_out_3), .out_6(out_35),
    .in_3(manage_cubes_mirror_1_out_13), .out_5(out_34));
  tand_l tand_l_18 (.out_3(tand_l_18_out_3), .in_1(out_34), .in_2(in_7));
  tand_l tand_l_19 (.out_3(tand_l_19_out_3), .in_1(out_36), .in_2(in_8));
  tile_lock tile_lock_8 (
    .set(in_8), .reset(buffer_1_out), .enable(tor_6_out_3), .out_6(out_37),
    .in_3(manage_cubes_mirror_1_out_14), .out_5(out_36));
  tile_lock tile_lock_9 (
    .set(in_9), .reset(buffer_1_out), .enable(tor_6_out_3), .out_6(out_39),
    .in_3(manage_cubes_mirror_1_out_15), .out_5(out_38));
  tand_l tand_l_20 (.out_3(tand_l_20_out_3), .in_1(out_38), .in_2(in_9));
  tand_l tand_l_21 (.out_3(tand_l_21_out_3), .in_1(out_40), .in_2(in_10));
  tile_lock tile_lock_10 (
    .set(in_10), .reset(buffer_1_out), .enable(tor_6_out_3), .out_6(out_41),
    .in_3(manage_cubes_mirror_1_out_16), .out_5(out_40));
  tand_l tand_l_22 (.out_3(tand_l_22_out_3), .in_1(out_42), .in_2(in_11));
  tile_lock tile_lock_11 (
    .set(in_11), .reset(buffer_1_out), .enable(tor_6_out_3), .out_6(out_43),
    .in_3(manage_cubes_mirror_1_out_17), .out_5(out_42));
  buf buffer_1 (buffer_1_out, buffer_2_out);
  tor tor_6 (.in_1(reset), .in_2(enable), .out_3(tor_6_out_3));
  buf buffer_2 (buffer_2_out, reset);
  tt tt_6 (.in_1(tor_7_out_3), .out_2(roll_enabled));
  tor tor_7 (.in_1(tor_l_1_out_3), .in_2(tand_1_out_3), .out_3(tor_7_out_3));
  not not_2 (not_2_out, out_47);
  not not_3 (not_3_out, out_49);
  not not_4 (not_4_out, out_51);
  not not_5 (not_5_out, out_53);
  not not_6 (not_6_out, out_55);
  niceSR nicesr_1 (.set(and_1_out), .reset(not_7_out), .out_3(nicesr_1_out_3));
  not not_7 (not_7_out, enable);
  manage_cubes_mirror manage_cubes_mirror_1 (
    .in_1(out_46), .in_2(out_48), .in_3(out_50), .in_4(out_52), .in_5(out_54),
    .out_7(manage_cubes_mirror_1_out_7), .out_8(manage_cubes_mirror_1_out_8),
    .out_9(manage_cubes_mirror_1_out_9), .out_10(manage_cubes_mirror_1_out_10),
    .out_11(manage_cubes_mirror_1_out_11), .out_12(manage_cubes_mirror_1_out_12),
    .out_13(manage_cubes_mirror_1_out_13), .out_14(manage_cubes_mirror_1_out_14),
    .out_15(manage_cubes_mirror_1_out_15), .out_16(manage_cubes_mirror_1_out_16),
    .out_17(manage_cubes_mirror_1_out_17), .enable(enable));
  tor tor_8 (.in_1(other_done), .in_2(start), .out_3(tor_8_out_3));
  tor_l tor_l_1 (.out_3(tor_l_1_out_3), .in_1(tor_8_out_3), .in_2(counter_1_carry));
  Counter #(.width(2), .max('h3)) counter_1 (
    .carry(counter_1_carry), .clk(and_1_out), .clr(tor_9_out_3));  // open: load, D, count, Q
  and and_1 (and_1_out, roll_enabled, roll);
  tor tor_9 (.in_1(done), .in_2(counter_1_carry), .out_3(tor_9_out_3));
  // Probe on out_46
  player_panel player_panel_1 (
    .in_2(not_2_out), .out_9(out_46), .out_10(out_48), .out_11(out_50), .out_12(out_52), .out_13(out_54),
    .Roll(and_1_out), .in_3(not_3_out), .in_4(not_4_out), .in_5(not_5_out), .in_6(not_6_out),
    .Enable(enable), .Enable_cubes(nicesr_1_out_3));
  // Probe on out_48
  // Probe on out_50
  // Probe on out_52
  // Probe on out_54

  // Other names for the same wires on the sheet: _1 = out_47; _2 = out_49; _3 = out_51; _4 = out_53; _5 = out_55;
  //   _11[2:0] = out_46; _12[2:0] = out_48; _13[2:0] = out_50; _14[2:0] = out_52; _15[2:0] = out_54; a01 = out_22;
  //   a02 = out_24; a03 = out_26; a04 = out_28; a05 = out_30; a06 = out_32; a07 = out_34; a08 = out_36; a09 = out_38;
  //   a10 = out_40; a11 = out_42; p01[7:0] = out_23; p02[7:0] = out_25; p03[7:0] = out_27; p04[7:0] = out_29;
  //   p05[7:0] = out_31; p06[7:0] = out_33; p07[7:0] = out_35; p08[7:0] = out_37; p09[7:0] = out_39;
  //   p10[7:0] = out_41; p11[7:0] = out_43; s01 = in_1; s02 = in_2; s03 = in_3; s04 = in_4; s05 = in_5; s06 = in_6;
  //   s07 = in_7; s08 = in_8; s09 = in_9; s10 = in_10; s11 = in_11
endmodule

module tt_fancy (
  input  in_1,
  input  in_2,
  output out_3
);

  T_Flip_Flop t_ff_1 (.clk(in_1), .T(in_1), .Q(out_3), .reset(in_2));  // open: Qn, preset, en
endmodule

module tick (
  input  in_1,
  output out_2
);

  Counter #(.width(1), .max('h1)) counter_1 (.carry(out_2), .clk(in_1), .clr(out_2));  // open: load, D, count, Q
endmodule

module sum_points (
  input  in_1,
  input  in_2,
  input  in_3,
  input  in_4,
  input  in_5,
  input  in_6,
  input  in_7,
  input  in_8,
  input  in_9,
  input  in_10,
  input  in_11,
  input  [7:0] in_12,
  input  [7:0] in_13,
  input  [7:0] in_14,
  input  [7:0] in_15,
  input  [7:0] in_16,
  input  [7:0] in_17,
  input  [7:0] in_18,
  input  [7:0] in_19,
  input  [7:0] in_20,
  input  [7:0] in_21,
  input  [7:0] in_22,
  output [15:0] out_23
);

  wire not_1_out, not_2_out, not_3_out, not_4_out, not_5_out, not_6_out, not_7_out, not_8_out, not_9_out,
       not_10_out, not_11_out;
  wire [15:0] adder_1_out, adder_2_out, adder_3_out, adder_4_out, adder_5_out, adder_6_out, adder_7_out,
       adder_8_out, adder_9_out, bit_extender_1_out, bit_extender_2_out, bit_extender_3_out,
       bit_extender_4_out, bit_extender_5_out, bit_extender_6_out, bit_extender_7_out, bit_extender_8_out,
       bit_extender_9_out, bit_extender_10_out, bit_extender_11_out, multiplier_1_out, multiplier_2_out,
       multiplier_3_out, multiplier_4_out, multiplier_5_out, multiplier_6_out, multiplier_7_out,
       multiplier_8_out, multiplier_9_out, multiplier_10_out, multiplier_11_out, p00, p01, p02, p03, p04,
       p05, p06, p07, p08, p09, p10;

  not not_1 (not_1_out, in_1);
  not not_2 (not_2_out, in_2);
  not not_3 (not_3_out, in_3);
  not not_4 (not_4_out, in_4);
  not not_5 (not_5_out, in_5);
  not not_6 (not_6_out, in_6);
  not not_7 (not_7_out, in_7);
  not not_8 (not_8_out, in_8);
  not not_9 (not_9_out, in_9);
  not not_10 (not_10_out, in_10);
  not not_11 (not_11_out, in_11);
  assign bit_extender_1_out = {{15{1'b0}}, not_1_out};  // Bit_Extender bit_extender_1
  assign bit_extender_2_out = {{15{1'b0}}, not_2_out};  // Bit_Extender bit_extender_2
  assign bit_extender_3_out = {{15{1'b0}}, not_3_out};  // Bit_Extender bit_extender_3
  assign bit_extender_4_out = {{15{1'b0}}, not_4_out};  // Bit_Extender bit_extender_4
  // Probe on bit_extender_4_out
  assign bit_extender_5_out = {{15{1'b0}}, not_5_out};  // Bit_Extender bit_extender_5
  assign bit_extender_6_out = {{15{1'b0}}, not_6_out};  // Bit_Extender bit_extender_6
  assign bit_extender_7_out = {{15{1'b0}}, not_7_out};  // Bit_Extender bit_extender_7
  assign bit_extender_8_out = {{15{1'b0}}, not_8_out};  // Bit_Extender bit_extender_8
  assign bit_extender_9_out = {{15{1'b0}}, not_9_out};  // Bit_Extender bit_extender_9
  assign bit_extender_10_out = {{15{1'b0}}, not_10_out};  // Bit_Extender bit_extender_10
  assign bit_extender_11_out = {{15{1'b0}}, not_11_out};  // Bit_Extender bit_extender_11
  assign p00 = {{8{1'b0}}, in_12};  // Bit_Extender bit_extender_12
  assign p01 = {{8{1'b0}}, in_13};  // Bit_Extender bit_extender_13
  assign p02 = {{8{1'b0}}, in_14};  // Bit_Extender bit_extender_14
  assign p03 = {{8{1'b0}}, in_15};  // Bit_Extender bit_extender_15
  assign p04 = {{8{1'b0}}, in_16};  // Bit_Extender bit_extender_16
  assign p05 = {{8{1'b0}}, in_17};  // Bit_Extender bit_extender_17
  assign p06 = {{8{1'b0}}, in_18};  // Bit_Extender bit_extender_18
  assign p07 = {{8{1'b0}}, in_19};  // Bit_Extender bit_extender_19
  assign p08 = {{8{1'b0}}, in_20};  // Bit_Extender bit_extender_20
  assign p09 = {{8{1'b0}}, in_21};  // Bit_Extender bit_extender_21
  assign p10 = {{8{1'b0}}, in_22};  // Bit_Extender bit_extender_22
  Multiplier #(.width(16)) multiplier_1 (
    .a(bit_extender_7_out), .b(p06), .out(multiplier_1_out), .cin({16{1'b0}}));  // open: cout
  Multiplier #(.width(16)) multiplier_2 (
    .a(bit_extender_8_out), .b(p07), .out(multiplier_2_out), .cin({16{1'b0}}));  // open: cout
  Multiplier #(.width(16)) multiplier_3 (
    .a(bit_extender_9_out), .b(p08), .out(multiplier_3_out), .cin({16{1'b0}}));  // open: cout
  Multiplier #(.width(16)) multiplier_4 (
    .a(bit_extender_10_out), .b(p09), .out(multiplier_4_out), .cin({16{1'b0}}));  // open: cout
  Multiplier #(.width(16)) multiplier_5 (
    .a(bit_extender_11_out), .b(p10), .out(multiplier_5_out), .cin({16{1'b0}}));  // open: cout
  Multiplier #(.width(16)) multiplier_6 (
    .a(bit_extender_1_out), .b(p00), .out(multiplier_6_out), .cin({16{1'b0}}));  // open: cout
  Multiplier #(.width(16)) multiplier_7 (
    .a(bit_extender_2_out), .b(p01), .out(multiplier_7_out), .cin({16{1'b0}}));  // open: cout
  Multiplier #(.width(16)) multiplier_8 (
    .a(bit_extender_3_out), .b(p02), .out(multiplier_8_out), .cin({16{1'b0}}));  // open: cout
  Multiplier #(.width(16)) multiplier_9 (
    .a(bit_extender_4_out), .b(p03), .out(multiplier_9_out), .cin({16{1'b0}}));  // open: cout
  Multiplier #(.width(16)) multiplier_10 (
    .a(bit_extender_5_out), .b(p04), .out(multiplier_10_out), .cin({16{1'b0}}));  // open: cout
  Multiplier #(.width(16)) multiplier_11 (
    .a(bit_extender_6_out), .b(p05), .out(multiplier_11_out), .cin({16{1'b0}}));  // open: cout
  // Probe on multiplier_8_out
  // Probe on multiplier_9_out
  Adder #(.width(16)) adder_1 (
    .a(multiplier_6_out), .b(multiplier_7_out), .out(adder_1_out), .cin(1'b0));  // open: cout
  Adder #(.width(16)) adder_2 (
    .a(multiplier_8_out), .b(multiplier_9_out), .out(adder_2_out), .cin(1'b0));  // open: cout
  Adder #(.width(16)) adder_3 (.a(adder_1_out), .b(adder_2_out), .out(adder_3_out), .cin(1'b0));  // open: cout
  Adder #(.width(16)) adder_4 (
    .a(multiplier_10_out), .b(multiplier_11_out), .out(adder_4_out), .cin(1'b0));  // open: cout
  Adder #(.width(16)) adder_5 (
    .a(multiplier_1_out), .b(multiplier_2_out), .out(adder_5_out), .cin(1'b0));  // open: cout
  // Probe on adder_3_out
  Adder #(.width(16)) adder_6 (.a(adder_4_out), .b(adder_5_out), .out(adder_6_out), .cin(1'b0));  // open: cout
  Adder #(.width(16)) adder_7 (
    .a(multiplier_3_out), .b(multiplier_4_out), .out(adder_7_out), .cin(1'b0));  // open: cout
  Adder #(.width(16)) adder_8 (.a(adder_7_out), .b(multiplier_5_out), .out(adder_8_out), .cin(1'b0));  // open: cout
  Adder #(.width(16)) adder_9 (.a(adder_3_out), .b(adder_6_out), .out(adder_9_out), .cin(1'b0));  // open: cout
  // Probe on adder_9_out
  Adder #(.width(16)) adder_10 (.a(adder_9_out), .b(adder_8_out), .out(out_23), .cin(1'b0));  // open: cout
  // Probe on out_23
  // Probe on adder_8_out
endmodule
